// Digital circuit simulation copy.dig as structural Verilog
module simulation_copy (
  input  NE555___ext_CLK__to_do,
  input  Int_NE555,
  input  clk_3,
  output not_CLR,
  output CLK,
  output not_CLK,
  output a0,
  output a1,
  output a2,
  output a3,
  output a4,
  output a5,
  output LRALU_IN,
  output LRALU_OUT,
  output ALUS0,
  output ALUS1,
  output ALUS2,
  output ALUS3,
  output ALUCN,
  output ALUM,
  output not_ERALU_OUT,
  output a7,
  output a0_2,
  output a1_2,
  output a2_2,
  output a3_2,
  output LC,
  output CHKZ,
  output CHKC,
  output not_CLC,
  output not_SEC,
  output LZN,
  output a2_3,
  output CHKN,
  output a4_2,
  output a5_2,
  output a6,
  output a7_2,
  output a0_3,
  output a1_3,
  output a2_4,
  output a3_3,
  output LO,
  output CHKO,
  output EFR_out,
  output EFR_in,
  output not_CLR_2,
  output not_HLT,
  output CLK_2,
  output not_CLK_2,
  output CLR__not_used,
  output EEPROM_ready,
  output not_JMP,
  output LIR,
  output CHKI,
  output not_HLT_2,
  output not_ENA_I,
  output not_DIS_I,
  output not_NOP,
  output LINT_MASK,
  output EINT_OUT,
  output Reset_IRs,
  output Load_next_IR,
  output Inc_T,
  output Reset_T,
  output INT1,
  output INT2,
  output not_EA,
  output not_EX,
  output not_EY,
  output not_ETMP,
  output not_ED,
  output not_EE,
  output LA,
  output LX,
  output LY,
  output LTMP,
  output LD,
  output LE,
  output LOUT,
  output Enable_next_IR,
  output ESP,
  output EPC_ADDR,
  output CPC,
  output not_EPC_L,
  output not_EPC_H,
  output not_EPC_PAGE,
  output [23:0] Addr,
  output [7:0] Data,
  output [15:0] Ctrl,
  output notCSP,
  output SPD,
  output not_LPC_L,
  output COL0,
  output ROW0,
  output COL1,
  output COL2,
  output COL3,
  output COL4,
  output COL5,
  output COL6,
  output COL7,
  output ROW1,
  output ROW2,
  output ROW3,
  output ROW4,
  output ROW5,
  output ROW6,
  output ROW7,
  output KEYB_INT,
  output not_Memory_ADDR_Valid,
  output not_Memory_WRITE___READ,
  output ERAM,
  output WRAM,
  output EMAR,
  output LMAR_L,
  output LMAR_H,
  output LMAR_PAGE,
  output LMAR_PAGEZERO,
  output Memory_PAGE_ZERO,
  output not_LPC_H,
  output not_LPC_PAGE,
  output not_LPC_H_plus_P0,
  output MEMADDRVALID,
  output LRALU_IN_2,
  output LRALU_OUT_2,
  output ALUS0_2,
  output ALUS1_2,
  output ALUCN_2,
  output ALUM_2,
  output ALUS2_2,
  output ALUS3_2,
  output CHKC_2,
  output CHKZ_2,
  output CHKN_2,
  output CHKO_2,
  output EFR_IN_2,
  output EFR_OUT_2,
  output ERALU_OUT,
  output LC_2,
  output LZN_2,
  output LO_2,
  output not_CLC_2,
  output SEC
);

  wire _0x0_pin19, _0x60_pin19, _7400_1_pin3, _7400_1_pin5, _7400_1_pin8, _7400_1_pin10, _7400_1_pin11,
       _7400_1_pin12, _7400_2_pin2, _7400_3_pin3, _7400_3_pin5, _7400_3_pin8, _7400_3_pin10, _7400_3_pin11,
       _7400_3_pin12, _7400_4_pin2, _7400_4_pin6, _7400_4_pin8, _7400_5_pin9, _7400_8_pin2, _7400_8_pin4,
       _7400_8_pin9, _7400_9_pin6, _7400_9_pin10, _7400_10_pin1, _7400_10_pin2, _7400_10_pin3, _7400_10_pin8,
       _7400_10_pin9, _7400_10_pin12, _7400_11_pin3, _7400_11_pin6, _7400_11_pin8, _7400_12_pin3,
       _7400_12_pin6, _7400_12_pin8, _7400_13_pin1, _7400_13_pin3, _7400_13_pin6, _7400_13_pin8,
       _7400_13_pin10, _7400_14_pin4, _7400_14_pin6, _7400_15_pin3, _7400_15_pin8, _7408_1_pin1,
       _7408_1_pin2, _7408_1_pin3, _7408_1_pin6, _7408_1_pin10, _7408_2_pin9, _7408_2_pin10, _7408_2_pin11,
       _7408_3_pin1, _7408_3_pin2, _7408_3_pin3, _7408_3_pin5, _7408_3_pin6, _7408_3_pin10, _7408_4_pin9,
       _7408_4_pin10, _7408_4_pin11, _7408_6_pin11, _7408_7_pin3, _7408_7_pin6, _7410_1_pin2, _7410_1_pin6,
       _7410_1_pin8, _7410_1_pin10, _7410_1_pin11, _74138_2_pin1, _74138_2_pin2, _74138_2_pin3,
       _74138_3_pin2, _74138_3_pin3, _74138_4_pin12, _74138_5_pin7, _74138_5_pin9, _74138_5_pin10,
       _74138_5_pin11, _74138_5_pin12, _74138_5_pin13, _74138_5_pin14, _74138_5_pin15, _74138_6_pin7,
       _74138_6_pin9, _74138_6_pin10, _74138_6_pin11, _74138_6_pin12, _74138_6_pin13, _74138_6_pin14,
       _74138_6_pin15, _74161_1_pin15, _74161_2_pin15, _74161_3_pin15, _74161_4_pin15, _74161_5_pin15,
       _74163_1_pin7, _74163_1_pin12, _74163_1_pin13, _74163_1_pin14, _74163_2_pin12, _74163_2_pin13,
       _74163_2_pin14, _74238_1_pin1, _74238_1_pin2, _74238_1_pin3, _74245_1_pin19, _74245_2_pin19,
       _74373_1_pin2, _74373_1_pin6, _74373_1_pin9, _74373_1_pin12, _74373_2_pin8, _74373_2_pin13,
       _74373_2_pin14, _74373_2_pin17, _74373_3_pin8, _74373_3_pin13, _74373_4_pin8, _74373_4_pin13,
       _74373_4_pin14, _74373_4_pin17, _74540_1_pin11, _74540_1_pin12, _74540_1_pin13, _74540_1_pin14,
       _74540_1_pin15, _74540_1_pin16, _74540_1_pin17, _74540_1_pin18, _74688_1_pin3, _74688_1_pin5,
       _74688_1_pin7, _74688_1_pin9, _74688_1_pin12, _74688_1_pin14, _74688_1_pin16, _74688_1_pin18,
       ALU_Control_Word_p19, ALU_Control_Word_p21, ALU_Control_Word_p22, ALU_Control_Word_p23, ALU_H_2_pin2,
       ALU_H_2_pin7, ALU_H_2_pin9, ALU_H_2_pin10, ALU_H_2_pin11, ALU_H_pin2, ALU_H_pin7, ALU_H_pin9,
       ALU_H_pin10, ALU_H_pin11, ALU_L_2_pin2, ALU_L_2_pin9, ALU_L_2_pin10, ALU_L_2_pin11, ALU_L_pin2,
       ALU_L_pin9, ALU_L_pin10, ALU_L_pin11, CLOCK_BUF_pin2, CLOCK_BUF_pin8, CLOCK_BUF_pin11,
       CLOCK_BUF_pin13, Debouncer_2_pin2, Debouncer_2_pin3, Debouncer_2_pin8, Debouncer_2_pin10,
       Debouncer_2_pin11, Debouncer_2_pin12, Debouncer_pin8, Debouncer_pin10, ext_I1_I2_pin5, ext_I1_I2_pin9,
       FR_in_2_pin9, FR_in_2_pin11, FR_in_2_pin12, FR_in_2_pin14, FR_in_pin9, FR_in_pin11, FR_in_pin12,
       FR_in_pin14, I_pin5, I_pin9, I_pin11, IC_L_pin15, Instructions_Control_Word_p17,
       Instructions_Control_Word_p19, Instructions_Control_Word_p20, Instructions_Control_Word_p21,
       INT_MASK_pin2, INT_MASK_pin5, INT_MASK_pin6, INT_MASK_pin9, keyb_timer_pin5, keyb_timer_pin6,
       keyb_timer_pin8, keyb_timer_pin9, MAR_H_pin11, MAR_L_pin11, MAR_PAGE_pin1, MAR_PAGE_pin2,
       MAR_PAGE_pin5, MAR_PAGE_pin6, MAR_PAGE_pin9, MAR_PAGE_pin11, MAR_PAGE_pin12, MAR_PAGE_pin15,
       MAR_PAGE_pin16, MAR_PAGE_pin19, N___O_2_pin3, N___O_pin3, Next_IR_pin2, Next_IR_pin5, Next_IR_pin6,
       Next_IR_pin9, Next_IR_pin12, Next_IR_pin15, Next_IR_pin16, Next_IR_pin19, PC_SP_Control_Word_p17,
       PC_SP_Control_Word_p19, PC_SP_Control_Word_p20, PC_SP_Control_Word_p21, RALU_IN_2_pin5,
       RALU_IN_2_pin6, RALU_IN_2_pin9, RALU_IN_2_pin15, RALU_IN_2_pin16, RALU_IN_2_pin19, RALU_IN_pin5,
       RALU_IN_pin6, RALU_IN_pin9, RALU_IN_pin15, RALU_IN_pin16, RALU_IN_pin19, RALU_OUT_2_pin8,
       RALU_OUT_2_pin18, RALU_OUT_pin8, RALU_OUT_pin18, RAM_L_2_p23, RAM_L_p21, RAM_L_p23, RAM_p3, RAM_p13,
       RAM_p17, Registers_Control_Word_p18, Registers_Control_Word_p19, Registers_Control_Word_p20,
       ROM__1st_8k_p19, ROM__2nd_8k_p19, ROM__3rd_8k_p19, SPhh_pin4, SPl_pin13, switchdt_1_p2, switchdt_1_p3,
       switchdt_2_p2, switchdt_2_p3, switchdt_3_p2, switchdt_3_p3, switchdt_6_p1, switchdt_14_p1,
       switchdt_22_p1, switchdt_30_p1, switchdt_38_p1, switchdt_46_p1, switchdt_54_p1, switchdt_62_p1,
       XOR_pin3, XOR_pin6, XOR_pin8, XOR_pin11;
  wire [3:0] _74161_1_pin14, _74161_2_pin14, _74161_3_pin14, _74161_4_pin14, _74161_5_pin14, _74161_6_pin14,
       _74245_3_pin3, _74245_4_pin5, _74245_4_pin9, OUT_pin2, OUT_pin12;

  // _28c64 Control_Word__6: pin names not known; wires that end beside it: 1'b0, a2_4, a1_3, a0_3, Ctrl[0], EFR_in, Ctrl[1], 1'b0, Ctrl[2], Ctrl[13], Ctrl[3], 1'b0, Ctrl[4], Ctrl[14], Ctrl[8], Ctrl[12], Ctrl[9], Ctrl[11], Ctrl[10], Ctrl[15], 1'b1, 1'b1
  // _28c64 Control_Word__5: pin names not known; wires that end beside it: 1'b0, a2_3, LZN, not_SEC, Ctrl[0], a7_2, Ctrl[1], 1'b0, Ctrl[2], Ctrl[13], Ctrl[3], 1'b0, Ctrl[4], Ctrl[14], Ctrl[8], Ctrl[12], Ctrl[9], Ctrl[11], Ctrl[10], Ctrl[15], 1'b1, 1'b1
  _7408 _7408_1 (
    .pin1(_7408_1_pin1), .pin2(_7408_1_pin2), .pin3(_7408_1_pin3), .pin4(CLK), .pin5(LO),
    .pin6(_7408_1_pin6), .pin7(1'b0), .pin8(not_JMP), .pin9(_7408_1_pin3), .pin10(_7408_1_pin10),
    .pin12(1'b1), .pin13(1'b1), .pin14(1'b1));  // open: pin11
  // _28c64 Control_Word__4: pin names not known; wires that end beside it: 1'b0, a2_2, a1_2, a0_2, Ctrl[0], not_CLC, Ctrl[1], 1'b0, Ctrl[2], Ctrl[13], Ctrl[3], 1'b0, Ctrl[4], Ctrl[14], Ctrl[8], Ctrl[12], Ctrl[9], Ctrl[11], Ctrl[10], Ctrl[15], 1'b1, 1'b1
  _74157 FR_in (
    .pin1(EFR_in), .pin2(1'b1), .pin3(1'b1), .pin5(1'b1), .pin6(1'b1), .pin8(1'b0), .pin9(FR_in_pin9),
    .pin10(Data[2]), .pin11(FR_in_pin11), .pin12(FR_in_pin12), .pin13(Data[3]), .pin14(FR_in_pin14),
    .pin15(1'b0), .pin16(1'b1));  // open: pin4, pin7
  _7400 _7400_1 (
    .pin1(EFR_out), .pin2(1'b0), .pin3(_7400_1_pin3), .pin4(CHKO), .pin5(_7400_1_pin5), .pin6(_7408_1_pin2),
    .pin7(1'b0), .pin8(_7400_1_pin8), .pin9(CHKC), .pin10(_7400_1_pin10), .pin11(_7400_1_pin11),
    .pin12(_7400_1_pin12), .pin13(CHKZ), .pin14(1'b1));
  _7400 _7400_2 (
    .pin1(CHKN), .pin2(_7400_2_pin2), .pin3(_7408_1_pin10), .pin4(1'b1), .pin5(1'b1), .pin7(1'b0),
    .pin9(1'b1), .pin10(1'b1), .pin12(1'b1), .pin13(1'b1), .pin14(1'b1));  // open: pin6, pin8, pin11
  _7474 N___O (
    .pin1(1'b1), .pin2(Data[7]), .pin3(N___O_pin3), .pin4(1'b1), .pin5(_7400_2_pin2), .pin7(1'b0),
    .pin8(_7400_1_pin5), .pin10(1'b1), .pin11(_7408_1_pin6), .pin12(FR_in_pin11), .pin13(1'b1), .pin14(1'b1));  // open: pin6, pin9
  _74245 FR_OUT (
    .pin1(1'b1), .pin2(1'b1), .pin3(1'b1), .pin4(_7400_1_pin10), .pin5(_7400_1_pin12), .pin6(1'b1),
    .pin7(1'b1), .pin8(1'b1), .pin9(_7400_2_pin2), .pin10(1'b0), .pin11(Data[7]), .pin12(Data[6]),
    .pin13(Data[5]), .pin14(Data[4]), .pin15(Data[3]), .pin16(Data[2]), .pin17(Data[1]), .pin18(Data[0]),
    .pin19(_7400_1_pin3), .pin20(1'b1));
  _7408 _7408_2 (
    .pin1(_7400_1_pin11), .pin2(_7400_1_pin8), .pin3(_7408_1_pin1), .pin4(CLK), .pin5(LZN),
    .pin6(N___O_pin3), .pin7(1'b0), .pin8(FR_in_pin14), .pin9(_7408_2_pin9), .pin10(_7408_2_pin10),
    .pin11(_7408_2_pin11), .pin12(CLK), .pin13(LC), .pin14(1'b1));
  _7474 Z___C (
    .pin1(1'b1), .pin2(FR_in_pin12), .pin3(N___O_pin3), .pin4(1'b1), .pin5(_7400_1_pin12), .pin7(1'b0),
    .pin9(_7400_1_pin10), .pin10(not_SEC), .pin11(_7408_2_pin11), .pin12(FR_in_pin9), .pin13(not_CLC),
    .pin14(1'b1));  // open: pin6, pin8
  // _28c64 Control_Word__3: pin names not known; wires that end beside it: 1'b0, ALUS2, ALUS1, ALUS0, Ctrl[0], a7, Ctrl[1], 1'b0, Ctrl[2], Ctrl[13], Ctrl[3], 1'b0, Ctrl[4], Ctrl[14], Ctrl[8], Ctrl[12], Ctrl[9], Ctrl[11], Ctrl[10], Ctrl[15], 1'b1, 1'b1, 1'b0
  // _28c64 Control_Word__2: pin names not known; wires that end beside it: a2, a1, a0, Ctrl[0], LRALU_OUT, Ctrl[1], 1'b0, Ctrl[2], Ctrl[13], Ctrl[3], 1'b0, Ctrl[4], Ctrl[14], Ctrl[8], Ctrl[12], Ctrl[9], Ctrl[11], Ctrl[10], Ctrl[15], 1'b1, 1'b1
  _74181 ALU_L (
    .pin1(Data[0]), .pin2(ALU_L_pin2), .pin3(ALUS3), .pin4(ALUS2), .pin5(ALUS1), .pin6(ALUS0), .pin7(ALUCN),
    .pin8(ALUM), .pin9(ALU_L_pin9), .pin10(ALU_L_pin10), .pin11(ALU_L_pin11), .pin12(1'b0));  // open: pin13, pin14, pin15, pin16, pin17, pin18, pin19, pin20, pin21, pin22, pin23, pin24
  _74181 ALU_H (
    .pin1(Data[4]), .pin2(ALU_H_pin2), .pin3(ALUS3), .pin4(ALUS2), .pin5(ALUS1), .pin6(ALUS0),
    .pin7(ALU_H_pin7), .pin8(ALUM), .pin9(ALU_H_pin9), .pin10(ALU_H_pin10), .pin11(ALU_H_pin11), .pin12(1'b0));  // open: pin13, pin14, pin15, pin16, pin17, pin18, pin19, pin20, pin21, pin22, pin23, pin24
  _74373 RALU_IN (
    .pin1(1'b0), .pin2(ALU_L_pin2), .pin3(Data[0]), .pin4(Data[1]), .pin5(RALU_IN_pin5), .pin6(RALU_IN_pin6),
    .pin7(Data[2]), .pin8(Data[3]), .pin9(RALU_IN_pin9), .pin10(1'b0), .pin11(LRALU_IN), .pin12(ALU_H_pin2),
    .pin13(Data[4]), .pin14(Data[5]), .pin15(RALU_IN_pin15), .pin16(RALU_IN_pin16), .pin17(Data[6]),
    .pin18(Data[7]), .pin19(RALU_IN_pin19), .pin20(1'b1));
  _74373 RALU_OUT (
    .pin1(not_ERALU_OUT), .pin2(Data[0]), .pin3(ALU_L_pin9), .pin4(ALU_L_pin10), .pin5(Data[1]),
    .pin6(Data[2]), .pin7(ALU_L_pin11), .pin8(RALU_OUT_pin8), .pin9(Data[3]), .pin10(1'b0),
    .pin11(LRALU_OUT), .pin12(Data[4]), .pin13(ALU_H_pin9), .pin14(ALU_H_pin10), .pin15(Data[5]),
    .pin16(Data[6]), .pin17(ALU_H_pin11), .pin18(RALU_OUT_pin18), .pin19(Data[7]), .pin20(1'b1));
  _74273 MAR_PAGE (
    .pin1(MAR_PAGE_pin1), .pin2(MAR_PAGE_pin2), .pin3(Data[0]), .pin4(Data[1]), .pin5(MAR_PAGE_pin5),
    .pin6(MAR_PAGE_pin6), .pin7(Data[2]), .pin8(Data[3]), .pin9(MAR_PAGE_pin9), .pin10(1'b0),
    .pin11(MAR_PAGE_pin11), .pin12(MAR_PAGE_pin12), .pin13(Data[4]), .pin14(Data[5]), .pin15(MAR_PAGE_pin15),
    .pin16(MAR_PAGE_pin16), .pin17(Data[6]), .pin18(Data[7]), .pin19(MAR_PAGE_pin19), .pin20(1'b1));
  // _62256 RAM: pin names not known; wires that end beside it: 1'b1, Addr[14], RAM_p3, Addr[12], Addr[13], Addr[7], Addr[8], Addr[6], Addr[9], Addr[5], Addr[11], Addr[4], RAM_p13, Addr[3], Addr[10], Addr[2], RAM_p17, Addr[1], Data[7], Addr[0], Data[0]
  _74245 _74245_1 (
    .pin1(1'b1), .pin2(MAR_PAGE_pin2), .pin3(MAR_PAGE_pin5), .pin4(MAR_PAGE_pin6), .pin5(MAR_PAGE_pin9),
    .pin6(MAR_PAGE_pin12), .pin7(MAR_PAGE_pin15), .pin8(MAR_PAGE_pin16), .pin9(MAR_PAGE_pin19), .pin10(1'b0),
    .pin11(Addr[23]), .pin12(Addr[22]), .pin13(Addr[21]), .pin14(Addr[20]), .pin15(Addr[19]),
    .pin16(Addr[18]), .pin17(Addr[17]), .pin18(Addr[16]), .pin19(_74245_1_pin19), .pin20(1'b1));
  _7408 _7408_3 (
    .pin1(_7408_3_pin1), .pin2(_7408_3_pin2), .pin3(_7408_3_pin3), .pin4(CLK), .pin5(_7408_3_pin5),
    .pin6(_7408_3_pin6), .pin7(1'b0), .pin8(not_JMP), .pin9(_7408_3_pin3), .pin10(_7408_3_pin10),
    .pin12(1'b1), .pin13(1'b1), .pin14(1'b1));  // open: pin11
  _74373 MAR_H (
    .pin1(_74245_1_pin19), .pin2(Addr[8]), .pin3(Data[0]), .pin4(Data[1]), .pin5(Addr[9]), .pin6(Addr[10]),
    .pin7(Data[2]), .pin8(Data[3]), .pin9(Addr[11]), .pin10(1'b0), .pin11(MAR_H_pin11), .pin12(Addr[12]),
    .pin13(Data[4]), .pin14(Data[5]), .pin15(Addr[13]), .pin16(Addr[14]), .pin17(Data[6]), .pin18(Data[7]),
    .pin19(Addr[15]), .pin20(1'b1));
  // _28c64 ROM__3rd_8k: pin names not known; wires that end beside it: Data[1], Data[2], Data[3], 1'b0, 1'b1, 1'b1, Addr[12], Addr[7], Addr[8], Addr[6], Addr[9], Addr[5], Addr[11], Addr[4], RAM_p13, Addr[3], Addr[10], Addr[2], ROM__3rd_8k_p19, Addr[1], Data[7], Addr[0], Data[0]
  _74157 FR_in_2 (
    .pin1(EFR_IN_2), .pin2(1'b1), .pin3(1'b1), .pin5(1'b1), .pin6(1'b1), .pin8(1'b0), .pin9(FR_in_2_pin9),
    .pin10(Data[2]), .pin11(FR_in_2_pin11), .pin12(FR_in_2_pin12), .pin13(Data[3]), .pin14(FR_in_2_pin14),
    .pin15(1'b0), .pin16(1'b1));  // open: pin4, pin7
  _74373 _74373_1 (
    .pin1(1'b0), .pin2(_74373_1_pin2), .pin3(not_CLC_2), .pin4(LO_2), .pin5(_7408_3_pin5),
    .pin6(_74373_1_pin6), .pin7(LZN_2), .pin8(LC_2), .pin9(_74373_1_pin9), .pin10(1'b0),
    .pin11(EEPROM_ready), .pin12(_74373_1_pin12), .pin13(ERALU_OUT), .pin14(1'b1), .pin17(1'b1),
    .pin18(1'b1), .pin20(1'b1));  // open: pin15, pin16, pin19
  _7400 _7400_3 (
    .pin1(EFR_OUT_2), .pin2(EFR_OUT_2), .pin3(_7400_3_pin3), .pin4(CHKO_2), .pin5(_7400_3_pin5),
    .pin6(_7408_3_pin2), .pin7(1'b0), .pin8(_7400_3_pin8), .pin9(CHKC_2), .pin10(_7400_3_pin10),
    .pin11(_7400_3_pin11), .pin12(_7400_3_pin12), .pin13(CHKZ_2), .pin14(1'b1));
  _7400 _7400_4 (
    .pin1(CHKN_2), .pin2(_7400_4_pin2), .pin3(_7408_3_pin10), .pin4(_74373_1_pin12), .pin5(_74373_1_pin12),
    .pin6(_7400_4_pin6), .pin7(1'b0), .pin8(_7400_4_pin8), .pin9(SEC), .pin10(SEC), .pin12(1'b1),
    .pin13(1'b1), .pin14(1'b1));  // open: pin11
  _7474 N___O_2 (
    .pin1(1'b1), .pin2(Data[7]), .pin3(N___O_2_pin3), .pin4(1'b1), .pin5(_7400_4_pin2), .pin7(1'b0),
    .pin8(_7400_3_pin5), .pin10(1'b1), .pin11(_7408_3_pin6), .pin12(FR_in_2_pin11), .pin13(1'b1), .pin14(1'b1));  // open: pin6, pin9
  _74245 FR_OUT_2 (
    .pin1(1'b1), .pin2(1'b1), .pin3(1'b1), .pin4(_7400_3_pin10), .pin5(_7400_3_pin12), .pin6(1'b1),
    .pin7(1'b1), .pin8(1'b1), .pin9(_7400_4_pin2), .pin10(1'b0), .pin11(Data[7]), .pin12(Data[6]),
    .pin13(Data[5]), .pin14(Data[4]), .pin15(Data[3]), .pin16(Data[2]), .pin17(Data[1]), .pin18(Data[0]),
    .pin19(_7400_3_pin3), .pin20(1'b1));
  // _28c64 ROM__2nd_8k: pin names not known; wires that end beside it: Data[1], Data[2], Data[3], 1'b0, 1'b1, 1'b1, Addr[12], Addr[7], Addr[8], Addr[6], Addr[9], Addr[5], Addr[11], Addr[4], RAM_p13, Addr[3], Addr[10], Addr[2], ROM__2nd_8k_p19, Addr[1], Data[7], Addr[0], Data[0]
  _74373 MAR_L (
    .pin1(_74245_1_pin19), .pin2(Addr[0]), .pin3(Data[0]), .pin4(Data[1]), .pin5(Addr[1]), .pin6(Addr[2]),
    .pin7(Data[2]), .pin8(Data[3]), .pin9(Addr[3]), .pin10(1'b0), .pin11(MAR_L_pin11), .pin12(Addr[4]),
    .pin13(Data[4]), .pin14(Data[5]), .pin15(Addr[5]), .pin16(Addr[6]), .pin17(Data[6]), .pin18(Data[6]),
    .pin19(Addr[7]), .pin20(1'b1));
  _7408 _7408_4 (
    .pin1(_7400_3_pin11), .pin2(_7400_3_pin8), .pin3(_7408_3_pin1), .pin4(CLK), .pin5(_74373_1_pin6),
    .pin6(N___O_2_pin3), .pin7(1'b0), .pin8(FR_in_2_pin14), .pin9(_7408_4_pin9), .pin10(_7408_4_pin10),
    .pin11(_7408_4_pin11), .pin12(CLK), .pin13(_74373_1_pin9), .pin14(1'b1));
  _7474 Z___C_2 (
    .pin1(1'b1), .pin2(FR_in_2_pin12), .pin3(N___O_2_pin3), .pin4(1'b1), .pin5(_7400_3_pin12), .pin7(1'b0),
    .pin9(_7400_3_pin10), .pin10(_7400_4_pin8), .pin11(_7408_4_pin11), .pin12(FR_in_2_pin9),
    .pin13(_74373_1_pin2), .pin14(1'b1));  // open: pin6, pin8
  _74238 _74238_1 (
    .pin1(_74238_1_pin1), .pin2(_74238_1_pin2), .pin3(_74238_1_pin3), .pin4(1'b0), .pin5(1'b0),
    .pin6(EEPROM_ready), .pin7(SEC), .pin8(1'b0), .pin9(EFR_OUT_2), .pin10(EFR_IN_2), .pin11(CHKO_2),
    .pin12(CHKN_2), .pin13(CHKZ_2), .pin14(CHKC_2), .pin16(1'b1));  // open: pin15
  // _62256 RAM_L: pin names not known; wires that end beside it: Addr[14], Addr[12], Addr[7], Addr[6], Addr[5], Addr[4], Addr[3], Addr[2], Addr[1], Addr[0], Data[0], Data[1], Data[2], 1'b0, 1'b1, not_Memory_WRITE___READ, Addr[13], Addr[8], Addr[9], Addr[11], RAM_L_p21, Addr[10], RAM_L_p23, Data[7]
  // _28c64 Flags_Control_Word: pin names not known; wires that end beside it: 1'b1, 1'b1, Ctrl[15], Ctrl[10], Ctrl[11], Ctrl[9], Ctrl[12], Ctrl[8], Ctrl[14], Ctrl[4], 1'b0, Ctrl[3], Ctrl[13], Ctrl[2], 1'b0, Ctrl[1], _74238_1_pin3, Ctrl[0], not_CLC_2, LO_2
  // _28c64 ROM__1st_8k: pin names not known; wires that end beside it: Data[1], Data[2], Data[3], 1'b0, 1'b1, 1'b1, Addr[12], Addr[7], Addr[8], Addr[6], Addr[9], Addr[5], Addr[11], Addr[4], RAM_p13, Addr[3], Addr[10], Addr[2], ROM__1st_8k_p19, Addr[1], Data[7], Addr[0], Data[0], Data[1], Data[2], 1'b0
  _7408 _7408_5 (
    .pin1(1'b1), .pin2(1'b1), .pin4(CLK), .pin5(LMAR_PAGE), .pin6(MAR_PAGE_pin11), .pin7(1'b0),
    .pin8(MAR_H_pin11), .pin9(CLK), .pin10(LMAR_H), .pin11(MAR_L_pin11), .pin12(CLK), .pin13(LMAR_L),
    .pin14(1'b1));  // open: pin3
  _7400 _7400_5 (
    .pin1(Addr[15]), .pin2(Memory_PAGE_ZERO), .pin3(RAM_p17), .pin4(MEMADDRVALID), .pin5(EEPROM_ready),
    .pin6(not_Memory_ADDR_Valid), .pin7(1'b0), .pin8(Memory_PAGE_ZERO), .pin9(_7400_5_pin9),
    .pin10(_7400_5_pin9), .pin11(not_Memory_WRITE___READ), .pin12(WRAM), .pin13(WRAM), .pin14(1'b1));
  // _62256 RAM_L_2: pin names not known; wires that end beside it: Addr[14], Addr[12], Addr[7], Addr[6], Addr[5], Addr[4], Addr[3], Addr[2], Addr[1], Addr[0], Data[0], Data[1], Data[2], 1'b0, 1'b1, not_Memory_WRITE___READ, Addr[13], Addr[8], Addr[9], Addr[11], RAM_L_p21, Addr[10], RAM_L_2_p23, Data[7]
  // _28c64 ALU_Control_Word: pin names not known; wires that end beside it: LZN_2, 1'b0, 1'b1, 1'b1, Ctrl[15], Ctrl[10], Ctrl[11], Ctrl[9], Ctrl[12], Ctrl[8], Ctrl[14], Ctrl[4], 1'b0, Ctrl[3], Ctrl[13], Ctrl[2], 1'b0, Ctrl[1], ALU_Control_Word_p19, Ctrl[0], ALU_Control_Word_p21, ALU_Control_Word_p22, ALU_Control_Word_p23, 1'b0
  _74181 ALU_L_2 (
    .pin1(Data[0]), .pin2(ALU_L_2_pin2), .pin3(ALUS3_2), .pin4(ALUS2_2), .pin5(ALUS1_2), .pin6(ALUS0_2),
    .pin7(ALUCN_2), .pin8(ALUM_2), .pin9(ALU_L_2_pin9), .pin10(ALU_L_2_pin10), .pin11(ALU_L_2_pin11),
    .pin12(1'b0));  // open: pin13, pin14, pin15, pin16, pin17, pin18, pin19, pin20, pin21, pin22, pin23, pin24
  _74181 ALU_H_2 (
    .pin1(Data[4]), .pin2(ALU_H_2_pin2), .pin3(ALUS3_2), .pin4(ALUS2_2), .pin5(ALUS1_2), .pin6(ALUS0_2),
    .pin7(ALU_H_2_pin7), .pin8(ALUM_2), .pin9(ALU_H_2_pin9), .pin10(ALU_H_2_pin10), .pin11(ALU_H_2_pin11),
    .pin12(1'b0));  // open: pin13, pin14, pin15, pin16, pin17, pin18, pin19, pin20, pin21, pin22, pin23, pin24
  _7400 _7400_6 (
    .pin1(EEPROM_ready), .pin2(ERAM), .pin3(RAM_p13), .pin4(LMAR_PAGEZERO), .pin5(EEPROM_ready),
    .pin6(MAR_PAGE_pin1), .pin7(1'b0), .pin8(RAM_p3), .pin9(WRAM), .pin10(CLK), .pin11(_74245_1_pin19),
    .pin12(EMAR), .pin13(EEPROM_ready), .pin14(1'b1));
  _74138 _74138_1 (
    .pin1(Addr[13]), .pin2(Addr[14]), .pin3(1'b0), .pin4(Addr[15]), .pin5(1'b0), .pin6(Memory_PAGE_ZERO),
    .pin8(1'b0), .pin13(ROM__3rd_8k_p19), .pin14(ROM__2nd_8k_p19), .pin15(ROM__1st_8k_p19), .pin16(1'b1));  // open: pin7, pin9, pin10, pin11, pin12
  _74688 ZEROPAGE (
    .pin1(1'b0), .pin2(1'b0), .pin3(Addr[16]), .pin4(1'b0), .pin5(Addr[17]), .pin6(1'b0), .pin7(Addr[18]),
    .pin8(1'b0), .pin9(Addr[19]), .pin10(1'b0), .pin11(1'b0), .pin12(Addr[20]), .pin13(1'b0),
    .pin14(Addr[21]), .pin15(1'b0), .pin16(Addr[22]), .pin17(1'b0), .pin18(Addr[23]), .pin19(_7400_5_pin9),
    .pin20(1'b1));
  _7400 _7400_7 (
    .pin1(not_Memory_WRITE___READ), .pin2(not_Memory_WRITE___READ), .pin3(RAM_L_p21), .pin4(1'b1),
    .pin5(1'b1), .pin7(1'b0), .pin9(1'b1), .pin10(1'b1), .pin12(1'b1), .pin13(1'b1), .pin14(1'b1));  // open: pin6, pin8, pin11
  _7400 _7400_8 (
    .pin1(Addr[15]), .pin2(_7400_8_pin2), .pin3(RAM_L_p23), .pin4(_7400_8_pin4), .pin5(_7400_8_pin2),
    .pin6(RAM_L_2_p23), .pin7(1'b0), .pin8(_7400_8_pin2), .pin9(_7400_8_pin9), .pin10(_7400_8_pin9),
    .pin11(_7400_8_pin4), .pin12(Addr[15]), .pin13(Addr[15]), .pin14(1'b1));
  // _28c64 Memory_Control_Word: pin names not known; wires that end beside it: 1'b1, 1'b1, Ctrl[15], Ctrl[10], Ctrl[11], Ctrl[9], Ctrl[12], Ctrl[8], Ctrl[14], Ctrl[4], 1'b0, Ctrl[3], Ctrl[13], Ctrl[2], 1'b0, Ctrl[1], ERAM, Ctrl[0], LMAR_L, LMAR_H, LMAR_PAGE, 1'b0
  _74373 RALU_IN_2 (
    .pin1(1'b0), .pin2(ALU_L_2_pin2), .pin3(Data[0]), .pin4(Data[1]), .pin5(RALU_IN_2_pin5),
    .pin6(RALU_IN_2_pin6), .pin7(Data[2]), .pin8(Data[3]), .pin9(RALU_IN_2_pin9), .pin10(1'b0),
    .pin11(LRALU_IN_2), .pin12(ALU_H_2_pin2), .pin13(Data[4]), .pin14(Data[5]), .pin15(RALU_IN_2_pin15),
    .pin16(RALU_IN_2_pin16), .pin17(Data[6]), .pin18(Data[7]), .pin19(RALU_IN_2_pin19), .pin20(1'b1));
  _74373 RALU_OUT_2 (
    .pin1(_7400_4_pin6), .pin2(Data[0]), .pin3(ALU_L_2_pin9), .pin4(ALU_L_2_pin10), .pin5(Data[1]),
    .pin6(Data[2]), .pin7(ALU_L_2_pin11), .pin8(RALU_OUT_2_pin8), .pin9(Data[3]), .pin10(1'b0),
    .pin11(LRALU_OUT_2), .pin12(Data[4]), .pin13(ALU_H_2_pin9), .pin14(ALU_H_2_pin10), .pin15(Data[5]),
    .pin16(Data[6]), .pin17(ALU_H_2_pin11), .pin18(RALU_OUT_2_pin18), .pin19(Data[7]), .pin20(1'b1));
  _74373 _74373_2 (
    .pin1(1'b0), .pin2(LRALU_IN_2), .pin3(ALU_Control_Word_p21), .pin4(ALU_Control_Word_p22),
    .pin5(LRALU_OUT_2), .pin6(ALUS0_2), .pin7(ALU_Control_Word_p23), .pin8(_74373_2_pin8), .pin9(ALUS1_2),
    .pin10(1'b0), .pin11(EEPROM_ready), .pin12(ALUS2_2), .pin13(_74373_2_pin13), .pin14(_74373_2_pin14),
    .pin15(ALUS3_2), .pin16(ALUCN_2), .pin17(_74373_2_pin17), .pin18(ALU_Control_Word_p19), .pin19(ALUM_2),
    .pin20(1'b1));
  _74688 _0x01 (
    .pin1(not_Memory_ADDR_Valid), .pin2(1'b1), .pin3(Addr[16]), .pin4(1'b0), .pin5(Addr[17]), .pin6(1'b0),
    .pin7(Addr[18]), .pin8(1'b0), .pin9(Addr[19]), .pin10(1'b0), .pin11(1'b0), .pin12(Addr[20]),
    .pin13(1'b0), .pin14(Addr[21]), .pin15(1'b0), .pin16(Addr[22]), .pin17(1'b0), .pin18(Addr[23]),
    .pin19(_7400_8_pin9), .pin20(1'b1));
  Seven_Seg_Hex seven_seg_hex_1 (.d(Data[7:4]), .dp(1'b0));
  Seven_Seg_Hex seven_seg_hex_2 (.d(Data[3:0]), .dp(1'b0));
  Seven_Seg_Hex seven_seg_hex_3 (.d(Addr[23:20]), .dp(1'b0));
  Seven_Seg_Hex seven_seg_hex_4 (.d(Addr[19:16]), .dp(1'b0));
  Seven_Seg_Hex seven_seg_hex_5 (.d(Addr[15:12]), .dp(1'b0));
  Seven_Seg_Hex seven_seg_hex_6 (.d(Addr[11:8]), .dp(1'b0));
  Seven_Seg_Hex seven_seg_hex_7 (.d(Addr[7:4]), .dp(1'b0));
  Seven_Seg_Hex seven_seg_hex_8 (.d(Addr[3:0]), .dp(1'b0));
  Seven_Seg_Hex seven_seg_hex_9 (.d(Ctrl[15:12]), .dp(1'b0));
  Seven_Seg_Hex seven_seg_hex_10 (.d(Ctrl[11:8]), .dp(1'b0));
  Seven_Seg_Hex seven_seg_hex_11 (.d({3'b000, Ctrl[4]}), .dp(1'b0));
  Seven_Seg_Hex seven_seg_hex_12 (.d(Ctrl[3:0]), .dp(1'b0));
  // SwitchDT switchdt_1: pin names not known; wires that end beside it: 1'b0, switchdt_1_p2, switchdt_1_p3
  // SwitchDT switchdt_2: pin names not known; wires that end beside it: 1'b0, switchdt_2_p2, switchdt_2_p3
  // SwitchDT switchdt_3: pin names not known; wires that end beside it: 1'b0, switchdt_3_p2, switchdt_3_p3
  // SwitchDT switchdt_4: pin names not known; wires that end beside it: INT1, 1'b1
  // _28c64 PC_SP_Control_Word: pin names not known; wires that end beside it: 1'b1, 1'b1, Ctrl[15], Ctrl[10], Ctrl[11], Ctrl[9], Ctrl[12], Ctrl[8], Ctrl[14], Ctrl[4], 1'b0, Ctrl[3], Ctrl[13], Ctrl[2], 1'b0, Ctrl[1], PC_SP_Control_Word_p17, Ctrl[0], PC_SP_Control_Word_p19, PC_SP_Control_Word_p20, PC_SP_Control_Word_p21, 1'b0
  // _28c64 Instructions_Control_Word: pin names not known; wires that end beside it: 1'b1, 1'b1, Ctrl[15], Ctrl[10], Ctrl[11], Ctrl[9], Ctrl[12], Ctrl[8], Ctrl[14], Ctrl[4], 1'b0, Ctrl[3], Ctrl[13], Ctrl[2], 1'b0, Ctrl[1], Instructions_Control_Word_p17, Ctrl[0], Instructions_Control_Word_p19, Instructions_Control_Word_p20, Instructions_Control_Word_p21, 1'b0
  // SwitchDT switchdt_5: pin names not known; wires that end beside it: INT2, 1'b1
  PullUp pullup_1 (.out(switchdt_1_p3));
  PullUp pullup_2 (.out(switchdt_2_p3));
  PullUp pullup_3 (.out(switchdt_3_p3));
  // _28c64 Registers_Control_Word: pin names not known; wires that end beside it: 1'b1, 1'b1, Ctrl[15], Ctrl[10], Ctrl[11], Ctrl[9], Ctrl[12], Ctrl[8], Ctrl[14], Ctrl[4], 1'b0, Ctrl[3], Ctrl[13], Ctrl[2], 1'b0, Ctrl[1], Ctrl[0], Registers_Control_Word_p18, Registers_Control_Word_p19, Registers_Control_Word_p20, 1'b0
  _74688 _0x0 (
    .pin1(not_Memory_ADDR_Valid), .pin2(1'b1), .pin3(not_Memory_WRITE___READ), .pin4(1'b1),
    .pin5(Memory_PAGE_ZERO), .pin6(1'b0), .pin7(1'b0), .pin8(1'b0), .pin9(Addr[3]), .pin10(1'b0),
    .pin11(1'b0), .pin12(Addr[4]), .pin13(1'b0), .pin14(Addr[5]), .pin15(1'b0), .pin16(Addr[6]),
    .pin17(1'b0), .pin18(Addr[7]), .pin19(_0x0_pin19), .pin20(1'b1));
  PullUp pullup_4 (.out(switchdt_1_p2));
  PullUp pullup_5 (.out(switchdt_2_p2));
  PullUp pullup_6 (.out(switchdt_3_p2));
  _74245 _74245_2 (
    .pin1(1'b1), .pin2(1'b0), .pin3(1'b0), .pin4(1'b0), .pin5(1'b0), .pin6(1'b0), .pin7(1'b0), .pin8(1'b0),
    .pin9(1'b0), .pin10(1'b0), .pin11(Addr[23]), .pin12(Addr[22]), .pin13(Addr[21]), .pin14(Addr[20]),
    .pin15(Addr[19]), .pin16(Addr[18]), .pin17(Addr[17]), .pin18(Addr[16]), .pin19(_74245_2_pin19),
    .pin20(1'b1));
  _74245 _74245_3 (
    .pin1(1'b1), .pin2(_74245_3_pin3[0]), .pin3(_74245_3_pin3[1]), .pin4(_74245_3_pin3[2]),
    .pin5(_74245_3_pin3[3]), .pin6(1'b1), .pin7(1'b1), .pin8(1'b1), .pin9(1'b1), .pin10(1'b0),
    .pin11(Addr[15]), .pin12(Addr[14]), .pin13(Addr[13]), .pin14(Addr[12]), .pin15(Addr[11]),
    .pin16(Addr[10]), .pin17(Addr[9]), .pin18(Addr[8]), .pin19(_74245_2_pin19), .pin20(1'b1));
  _74245 _74245_4 (
    .pin1(1'b1), .pin2(_74245_4_pin5[0]), .pin3(_74245_4_pin5[1]), .pin4(_74245_4_pin5[2]),
    .pin5(_74245_4_pin5[3]), .pin6(_74245_4_pin9[0]), .pin7(_74245_4_pin9[1]), .pin8(_74245_4_pin9[2]),
    .pin9(_74245_4_pin9[3]), .pin10(1'b0), .pin11(Addr[7]), .pin12(Addr[6]), .pin13(Addr[5]),
    .pin14(Addr[4]), .pin15(Addr[3]), .pin16(Addr[2]), .pin17(Addr[1]), .pin18(Addr[0]),
    .pin19(_74245_2_pin19), .pin20(1'b1));
  _7400 Debouncer (
    .pin1(switchdt_1_p2), .pin2(CLR__not_used), .pin3(not_CLR), .pin4(not_CLR), .pin5(switchdt_1_p3),
    .pin6(CLR__not_used), .pin7(1'b0), .pin8(Debouncer_pin8), .pin9(switchdt_2_p3), .pin10(Debouncer_pin10),
    .pin11(Debouncer_pin10), .pin12(Debouncer_pin8), .pin13(switchdt_2_p2), .pin14(1'b1));
  _7400 Debouncer_2 (
    .pin1(switchdt_3_p2), .pin2(Debouncer_2_pin2), .pin3(Debouncer_2_pin3), .pin4(Debouncer_2_pin3),
    .pin5(switchdt_3_p3), .pin6(Debouncer_2_pin2), .pin7(1'b0), .pin8(Debouncer_2_pin8),
    .pin9(Debouncer_2_pin2), .pin10(Debouncer_2_pin10), .pin11(Debouncer_2_pin11), .pin12(Debouncer_2_pin12),
    .pin13(Debouncer_2_pin8), .pin14(1'b1));
  _7404 CLOCK_BUF (
    .pin1(Debouncer_2_pin11), .pin2(CLOCK_BUF_pin2), .pin3(CLOCK_BUF_pin2), .pin4(CLK),
    .pin5(Debouncer_2_pin11), .pin6(Enable_next_IR), .pin7(1'b0), .pin8(CLOCK_BUF_pin8),
    .pin9(NE555___ext_CLK__to_do), .pin10(EEPROM_ready), .pin11(CLOCK_BUF_pin11), .pin12(CLOCK_BUF_pin11),
    .pin13(CLOCK_BUF_pin13), .pin14(1'b1));
  Seven_Seg_Hex seven_seg_hex_13 (.d(_74161_6_pin14), .dp(1'b0));
  Seven_Seg_Hex seven_seg_hex_14 (.d(_74161_5_pin14), .dp(1'b0));
  // SwitchDT switchdt_6: pin names not known; wires that end beside it: switchdt_6_p1, ROW0
  // SwitchDT switchdt_7: pin names not known; wires that end beside it: switchdt_6_p1, ROW1
  // SwitchDT switchdt_8: pin names not known; wires that end beside it: switchdt_6_p1, ROW2
  // SwitchDT switchdt_9: pin names not known; wires that end beside it: switchdt_6_p1, ROW3
  // SwitchDT switchdt_10: pin names not known; wires that end beside it: switchdt_6_p1, ROW4
  // SwitchDT switchdt_11: pin names not known; wires that end beside it: switchdt_6_p1, ROW5
  // SwitchDT switchdt_12: pin names not known; wires that end beside it: switchdt_6_p1, ROW6
  // SwitchDT switchdt_13: pin names not known; wires that end beside it: switchdt_6_p1, ROW7
  Seven_Seg_Hex seven_seg_hex_15 (.d(_74161_4_pin14), .dp(1'b0));
  _74688 _0x60 (
    .pin1(not_Memory_ADDR_Valid), .pin2(1'b0), .pin3(Addr[8]), .pin4(1'b0), .pin5(Addr[9]), .pin6(1'b0),
    .pin7(Addr[10]), .pin8(1'b0), .pin9(Addr[11]), .pin10(1'b0), .pin11(1'b0), .pin12(Addr[12]),
    .pin13(1'b1), .pin14(Addr[13]), .pin15(1'b1), .pin16(Addr[14]), .pin17(1'b0), .pin18(Addr[15]),
    .pin19(_0x60_pin19), .pin20(1'b1));
  // SwitchDT switchdt_14: pin names not known; wires that end beside it: switchdt_14_p1, ROW0
  // SwitchDT switchdt_15: pin names not known; wires that end beside it: switchdt_14_p1, ROW1
  // SwitchDT switchdt_16: pin names not known; wires that end beside it: switchdt_14_p1, ROW2
  // SwitchDT switchdt_17: pin names not known; wires that end beside it: switchdt_14_p1, ROW3
  // SwitchDT switchdt_18: pin names not known; wires that end beside it: switchdt_14_p1, ROW4
  // SwitchDT switchdt_19: pin names not known; wires that end beside it: switchdt_14_p1, ROW5
  // SwitchDT switchdt_20: pin names not known; wires that end beside it: switchdt_14_p1, ROW6
  // SwitchDT switchdt_21: pin names not known; wires that end beside it: switchdt_14_p1, ROW7
  Seven_Seg_Hex seven_seg_hex_16 (.d(_74161_3_pin14), .dp(1'b0));
  _7400 _7400_9 (
    .pin1(Debouncer_pin10), .pin2(Debouncer_2_pin3), .pin3(Debouncer_2_pin12), .pin4(Debouncer_2_pin11),
    .pin5(Debouncer_2_pin11), .pin6(_7400_9_pin6), .pin7(1'b0), .pin9(_7400_9_pin6), .pin10(_7400_9_pin10),
    .pin11(_7400_9_pin10), .pin12(NE555___ext_CLK__to_do), .pin13(NE555___ext_CLK__to_do), .pin14(1'b1));  // open: pin8
  _74107 _74107_1 (
    .pin1(not_HLT), .pin3(Debouncer_2_pin10), .pin4(not_HLT), .pin7(1'b0), .pin8(1'b0), .pin9(1'b0),
    .pin10(1'b0), .pin11(1'b0), .pin12(NE555___ext_CLK__to_do), .pin13(not_CLR), .pin14(1'b1));  // open: pin2, pin5, pin6
  // SwitchDT switchdt_22: pin names not known; wires that end beside it: switchdt_22_p1, ROW0
  // SwitchDT switchdt_23: pin names not known; wires that end beside it: switchdt_22_p1, ROW1
  // SwitchDT switchdt_24: pin names not known; wires that end beside it: switchdt_22_p1, ROW2
  // SwitchDT switchdt_25: pin names not known; wires that end beside it: switchdt_22_p1, ROW3
  // SwitchDT switchdt_26: pin names not known; wires that end beside it: switchdt_22_p1, ROW4
  // SwitchDT switchdt_27: pin names not known; wires that end beside it: switchdt_22_p1, ROW5
  // SwitchDT switchdt_28: pin names not known; wires that end beside it: switchdt_22_p1, ROW6
  // SwitchDT switchdt_29: pin names not known; wires that end beside it: switchdt_22_p1, ROW7
  Seven_Seg_Hex seven_seg_hex_17 (.d(_74161_2_pin14), .dp(1'b0));
  Seven_Seg_Hex seven_seg_hex_18 (.d(_74161_1_pin14), .dp(1'b0));
  // SwitchDT switchdt_30: pin names not known; wires that end beside it: switchdt_30_p1, ROW0
  // SwitchDT switchdt_31: pin names not known; wires that end beside it: switchdt_30_p1, ROW1
  // SwitchDT switchdt_32: pin names not known; wires that end beside it: switchdt_30_p1, ROW2
  // SwitchDT switchdt_33: pin names not known; wires that end beside it: switchdt_30_p1, ROW3
  // SwitchDT switchdt_34: pin names not known; wires that end beside it: switchdt_30_p1, ROW4
  // SwitchDT switchdt_35: pin names not known; wires that end beside it: switchdt_30_p1, ROW5
  // SwitchDT switchdt_36: pin names not known; wires that end beside it: switchdt_30_p1, ROW6
  // SwitchDT switchdt_37: pin names not known; wires that end beside it: switchdt_30_p1, ROW7
  // SwitchDT switchdt_38: pin names not known; wires that end beside it: switchdt_38_p1, ROW0
  // SwitchDT switchdt_39: pin names not known; wires that end beside it: switchdt_38_p1, ROW1
  // SwitchDT switchdt_40: pin names not known; wires that end beside it: switchdt_38_p1, ROW2
  // SwitchDT switchdt_41: pin names not known; wires that end beside it: switchdt_38_p1, ROW3
  // SwitchDT switchdt_42: pin names not known; wires that end beside it: switchdt_38_p1, ROW4
  // SwitchDT switchdt_43: pin names not known; wires that end beside it: switchdt_38_p1, ROW5
  // SwitchDT switchdt_44: pin names not known; wires that end beside it: switchdt_38_p1, ROW6
  // SwitchDT switchdt_45: pin names not known; wires that end beside it: switchdt_38_p1, ROW7
  _7474 _7474_1 (
    .pin1(1'b1), .pin2(1'b0), .pin3(Enable_next_IR), .pin4(CLOCK_BUF_pin8), .pin5(CLOCK_BUF_pin13),
    .pin7(1'b0), .pin10(1'b1), .pin11(1'b1), .pin12(1'b1), .pin13(1'b1), .pin14(1'b1));  // open: pin6, pin8, pin9
  _74373 _74373_3 (
    .pin1(1'b0), .pin2(ESP), .pin3(PC_SP_Control_Word_p19), .pin4(PC_SP_Control_Word_p20), .pin5(EPC_ADDR),
    .pin6(CPC), .pin7(PC_SP_Control_Word_p21), .pin8(_74373_3_pin8), .pin9(notCSP), .pin10(1'b0),
    .pin11(EEPROM_ready), .pin12(SPD), .pin13(_74373_3_pin13), .pin14(1'b1), .pin17(1'b1), .pin18(1'b1),
    .pin20(1'b1));  // open: pin15, pin16, pin19
  _74191 SPhh (
    .pin1(1'b1), .pin2(_74245_3_pin3[1]), .pin3(_74245_3_pin3[0]), .pin4(SPhh_pin4), .pin5(SPD),
    .pin6(_74245_3_pin3[2]), .pin7(_74245_3_pin3[3]), .pin8(1'b0), .pin9(1'b1), .pin10(1'b1),
    .pin11(not_CLR), .pin14(CLK), .pin15(1'b1), .pin16(1'b1));  // open: pin12, pin13
  _74191 SPl (
    .pin1(1'b1), .pin2(_74245_4_pin5[1]), .pin3(_74245_4_pin5[0]), .pin4(notCSP), .pin5(SPD),
    .pin6(_74245_4_pin5[2]), .pin7(_74245_4_pin5[3]), .pin8(1'b0), .pin9(1'b1), .pin10(1'b1),
    .pin11(not_CLR), .pin13(SPl_pin13), .pin14(CLK), .pin15(1'b1), .pin16(1'b1));  // open: pin12
  _74191 SPh (
    .pin1(1'b1), .pin2(_74245_4_pin9[1]), .pin3(_74245_4_pin9[0]), .pin4(SPl_pin13), .pin5(SPD),
    .pin6(_74245_4_pin9[2]), .pin7(_74245_4_pin9[3]), .pin8(1'b0), .pin9(1'b1), .pin10(1'b1),
    .pin11(not_CLR), .pin13(SPhh_pin4), .pin14(CLK), .pin15(1'b1), .pin16(1'b1));  // open: pin12
  // SwitchDT switchdt_46: pin names not known; wires that end beside it: switchdt_46_p1, ROW0
  // SwitchDT switchdt_47: pin names not known; wires that end beside it: switchdt_46_p1, ROW1
  // SwitchDT switchdt_48: pin names not known; wires that end beside it: switchdt_46_p1, ROW2
  // SwitchDT switchdt_49: pin names not known; wires that end beside it: switchdt_46_p1, ROW3
  // SwitchDT switchdt_50: pin names not known; wires that end beside it: switchdt_46_p1, ROW4
  // SwitchDT switchdt_51: pin names not known; wires that end beside it: switchdt_46_p1, ROW5
  // SwitchDT switchdt_52: pin names not known; wires that end beside it: switchdt_46_p1, ROW6
  // SwitchDT switchdt_53: pin names not known; wires that end beside it: switchdt_46_p1, ROW7
  Seven_Seg_Hex seven_seg_hex_19 (.d(_74245_3_pin3), .dp(1'b0));
  _74138 _74138_2 (
    .pin1(_74138_2_pin1), .pin2(_74138_2_pin2), .pin3(_74138_2_pin3), .pin4(1'b0), .pin5(1'b0),
    .pin6(EEPROM_ready), .pin8(1'b0), .pin9(not_EE), .pin10(not_ED), .pin11(not_ETMP), .pin12(not_EY),
    .pin13(not_EX), .pin14(not_EA), .pin16(1'b1));  // open: pin7, pin15
  _74238 _74238_2 (
    .pin1(Registers_Control_Word_p18), .pin2(Registers_Control_Word_p19), .pin3(Registers_Control_Word_p20),
    .pin4(1'b0), .pin5(1'b0), .pin6(CLK), .pin7(LOUT), .pin8(1'b0), .pin9(LE), .pin10(LD), .pin11(LTMP),
    .pin12(LY), .pin13(LX), .pin14(LA), .pin16(1'b1));  // open: pin15
  _74373 _74373_4 (
    .pin1(1'b0), .pin2(LIR), .pin3(Instructions_Control_Word_p19), .pin4(Instructions_Control_Word_p20),
    .pin5(CHKI), .pin6(not_HLT), .pin7(Instructions_Control_Word_p21), .pin8(_74373_4_pin8),
    .pin9(not_ENA_I), .pin10(1'b0), .pin11(EEPROM_ready), .pin12(LINT_MASK), .pin13(_74373_4_pin13),
    .pin14(_74373_4_pin14), .pin15(EINT_OUT), .pin16(not_DIS_I), .pin17(_74373_4_pin17),
    .pin18(Instructions_Control_Word_p17), .pin19(not_NOP), .pin20(1'b1));
  // SwitchDT switchdt_54: pin names not known; wires that end beside it: switchdt_54_p1, ROW0
  // SwitchDT switchdt_55: pin names not known; wires that end beside it: switchdt_54_p1, ROW1
  // SwitchDT switchdt_56: pin names not known; wires that end beside it: switchdt_54_p1, ROW2
  // SwitchDT switchdt_57: pin names not known; wires that end beside it: switchdt_54_p1, ROW3
  // SwitchDT switchdt_58: pin names not known; wires that end beside it: switchdt_54_p1, ROW4
  // SwitchDT switchdt_59: pin names not known; wires that end beside it: switchdt_54_p1, ROW5
  // SwitchDT switchdt_60: pin names not known; wires that end beside it: switchdt_54_p1, ROW6
  // SwitchDT switchdt_61: pin names not known; wires that end beside it: switchdt_54_p1, ROW7
  Seven_Seg_Hex seven_seg_hex_20 (.d(_74245_4_pin9), .dp(1'b0));
  _7400 _7400_10 (
    .pin1(_7400_10_pin1), .pin2(_7400_10_pin2), .pin3(_7400_10_pin3), .pin4(_7400_10_pin3),
    .pin5(_7400_10_pin3), .pin6(KEYB_INT), .pin7(1'b0), .pin8(_7400_10_pin8), .pin9(_7400_10_pin9),
    .pin10(_7400_10_pin9), .pin11(_7400_10_pin2), .pin12(_7400_10_pin12), .pin13(_7400_10_pin12), .pin14(1'b1));
  _74163 _74163_1 (
    .pin1(1'b1), .pin2(clk_3), .pin3(1'b0), .pin4(1'b0), .pin5(1'b0), .pin6(1'b0), .pin7(_74163_1_pin7),
    .pin8(1'b0), .pin9(1'b1), .pin10(1'b1), .pin12(_74163_1_pin12), .pin13(_74163_1_pin13),
    .pin14(_74163_1_pin14), .pin16(1'b1));  // open: pin11, pin15
  Seven_Seg_Hex seven_seg_hex_21 (.d(_74245_4_pin5), .dp(1'b0));
  // SwitchDT switchdt_62: pin names not known; wires that end beside it: switchdt_62_p1, ROW0
  // SwitchDT switchdt_63: pin names not known; wires that end beside it: switchdt_62_p1, ROW1
  // SwitchDT switchdt_64: pin names not known; wires that end beside it: switchdt_62_p1, ROW2
  // SwitchDT switchdt_65: pin names not known; wires that end beside it: switchdt_62_p1, ROW3
  // SwitchDT switchdt_66: pin names not known; wires that end beside it: switchdt_62_p1, ROW4
  // SwitchDT switchdt_67: pin names not known; wires that end beside it: switchdt_62_p1, ROW5
  // SwitchDT switchdt_68: pin names not known; wires that end beside it: switchdt_62_p1, ROW6
  // SwitchDT switchdt_69: pin names not known; wires that end beside it: switchdt_62_p1, ROW7
  _74138 _74138_3 (
    .pin1(PC_SP_Control_Word_p17), .pin2(_74138_3_pin2), .pin3(_74138_3_pin3), .pin4(1'b0), .pin5(1'b0),
    .pin6(EEPROM_ready), .pin7(not_LPC_H_plus_P0), .pin8(1'b0), .pin9(not_LPC_PAGE), .pin10(not_LPC_H),
    .pin11(not_LPC_L), .pin12(not_EPC_PAGE), .pin13(not_EPC_H), .pin14(not_EPC_L), .pin16(1'b1));  // open: pin15
  _7400 _7400_11 (
    .pin1(_0x60_pin19), .pin2(_0x60_pin19), .pin3(_7400_11_pin3), .pin4(_0x0_pin19), .pin5(_0x0_pin19),
    .pin6(_7400_11_pin6), .pin7(1'b0), .pin8(_7400_11_pin8), .pin9(_74163_1_pin7), .pin10(_74163_1_pin7),
    .pin11(_74163_1_pin7), .pin12(_7400_11_pin6), .pin13(_7400_11_pin3), .pin14(1'b1));
  Seven_Seg_Hex seven_seg_hex_22 (.d(OUT_pin12), .dp(1'b0));
  _74138 _74138_4 (
    .pin1(_74163_1_pin14), .pin2(_74163_1_pin13), .pin3(1'b0), .pin4(1'b0), .pin5(1'b0), .pin6(1'b1),
    .pin8(1'b0), .pin12(_74138_4_pin12), .pin13(_7400_10_pin12), .pin15(_7400_10_pin9), .pin16(1'b1));  // open: pin7, pin9, pin10, pin11, pin14
  _7400 XOR (
    .pin1(_74163_1_pin12), .pin2(_74138_4_pin12), .pin3(XOR_pin3), .pin4(_74163_1_pin12), .pin5(XOR_pin3),
    .pin6(XOR_pin6), .pin7(1'b0), .pin8(XOR_pin8), .pin9(XOR_pin3), .pin10(_74138_4_pin12),
    .pin11(XOR_pin11), .pin12(XOR_pin8), .pin13(XOR_pin6), .pin14(1'b1));
  Seven_Seg_Hex seven_seg_hex_23 (.d(OUT_pin2), .dp(1'b0));
  _7400 _7400_12 (
    .pin1(not_LPC_L), .pin2(not_LPC_L), .pin3(_7400_12_pin3), .pin4(_7400_12_pin3), .pin5(CLK),
    .pin6(_7400_12_pin6), .pin7(1'b0), .pin8(_7400_12_pin8), .pin9(EPC_ADDR), .pin10(EEPROM_ready),
    .pin11(_74245_2_pin19), .pin12(ESP), .pin13(EEPROM_ready), .pin14(1'b1));
  _7400 _7400_13 (
    .pin1(_7400_13_pin1), .pin2(_7400_13_pin1), .pin3(_7400_13_pin3), .pin4(_7400_13_pin3), .pin5(CLK),
    .pin6(_7400_13_pin6), .pin7(1'b0), .pin8(_7400_13_pin8), .pin9(CLK), .pin10(_7400_13_pin10),
    .pin11(_7400_13_pin10), .pin12(not_LPC_PAGE), .pin13(not_LPC_PAGE), .pin14(1'b1));
  _7408 _7408_6 (
    .pin1(1'b1), .pin2(1'b1), .pin4(not_LPC_H), .pin5(not_LPC_H_plus_P0), .pin6(_7400_13_pin1), .pin7(1'b0),
    .pin9(1'b1), .pin10(1'b1), .pin11(_7408_6_pin11), .pin12(not_LPC_H_plus_P0), .pin13(not_CLR), .pin14(1'b1));  // open: pin3, pin8
  _74163 _74163_2 (
    .pin1(1'b1), .pin2(_7400_10_pin8), .pin3(1'b0), .pin4(1'b0), .pin5(1'b0), .pin6(1'b0), .pin7(1'b1),
    .pin8(1'b0), .pin9(1'b1), .pin10(1'b1), .pin12(_74163_2_pin12), .pin13(_74163_2_pin13),
    .pin14(_74163_2_pin14), .pin16(1'b1));  // open: pin11, pin15
  _74373 A (
    .pin1(not_EA), .pin2(Data[0]), .pin3(Data[0]), .pin4(Data[1]), .pin5(Data[1]), .pin6(Data[2]),
    .pin7(Data[2]), .pin8(Data[3]), .pin9(Data[3]), .pin10(1'b0), .pin11(LA), .pin12(Data[4]),
    .pin13(Data[4]), .pin14(Data[5]), .pin15(Data[5]), .pin16(Data[6]), .pin17(Data[6]), .pin18(Data[7]),
    .pin19(Data[7]), .pin20(1'b1));
  _7408 _7408_7 (
    .pin1(not_CLR), .pin2(not_DIS_I), .pin3(_7408_7_pin3), .pin4(LIR), .pin5(not_CLR), .pin6(_7408_7_pin6),
    .pin7(1'b0), .pin8(Load_next_IR), .pin9(CLK), .pin10(_7408_7_pin6), .pin11(Reset_T), .pin12(not_NOP),
    .pin13(not_CLR), .pin14(1'b1));
  _7400 _7400_14 (
    .pin1(1'b1), .pin2(1'b1), .pin4(_7400_14_pin4), .pin5(_7400_14_pin4), .pin6(_7400_14_pin6), .pin7(1'b0),
    .pin8(_7400_14_pin4), .pin9(LINT_MASK), .pin10(CLK), .pin12(1'b1), .pin13(1'b1), .pin14(1'b1));  // open: pin3, pin11
  _7474 I (
    .pin1(_7408_7_pin3), .pin2(1'b1), .pin3(1'b0), .pin4(not_ENA_I), .pin5(I_pin5), .pin7(1'b0),
    .pin9(I_pin9), .pin10(1'b1), .pin11(I_pin11), .pin12(1'b1), .pin13(not_ENA_I), .pin14(1'b1));  // open: pin6, pin8
  _74373 INT_MASK (
    .pin1(1'b0), .pin2(INT_MASK_pin2), .pin3(Data[0]), .pin4(Data[1]), .pin5(INT_MASK_pin5),
    .pin6(INT_MASK_pin6), .pin7(Data[2]), .pin8(Data[3]), .pin9(INT_MASK_pin9), .pin10(1'b0),
    .pin11(_7400_14_pin6), .pin13(Data[4]), .pin14(Data[5]), .pin17(Data[6]), .pin18(Data[7]), .pin20(1'b1));  // open: pin12, pin15, pin16, pin19
  _74138 _74138_5 (
    .pin1(_74163_2_pin14), .pin2(_74163_2_pin13), .pin3(_74163_2_pin12), .pin4(1'b0), .pin5(1'b0),
    .pin6(1'b1), .pin7(_74138_5_pin7), .pin8(1'b0), .pin9(_74138_5_pin9), .pin10(_74138_5_pin10),
    .pin11(_74138_5_pin11), .pin12(_74138_5_pin12), .pin13(_74138_5_pin13), .pin14(_74138_5_pin14),
    .pin15(_74138_5_pin15), .pin16(1'b1));
  _74138 _74138_6 (
    .pin1(Addr[0]), .pin2(Addr[1]), .pin3(Addr[2]), .pin4(_0x60_pin19), .pin5(_0x0_pin19), .pin6(1'b1),
    .pin7(_74138_6_pin7), .pin8(1'b0), .pin9(_74138_6_pin9), .pin10(_74138_6_pin10), .pin11(_74138_6_pin11),
    .pin12(_74138_6_pin12), .pin13(_74138_6_pin13), .pin14(_74138_6_pin14), .pin15(_74138_6_pin15),
    .pin16(1'b1));
  _74373 X (
    .pin1(not_EX), .pin2(Data[0]), .pin3(Data[0]), .pin4(Data[1]), .pin5(Data[1]), .pin6(Data[2]),
    .pin7(Data[2]), .pin8(Data[3]), .pin9(Data[3]), .pin10(1'b0), .pin11(LX), .pin12(Data[4]),
    .pin13(Data[4]), .pin14(Data[5]), .pin15(Data[5]), .pin16(Data[6]), .pin17(Data[6]), .pin18(Data[7]),
    .pin19(Data[7]), .pin20(1'b1));
  _7474 keyb_timer (
    .pin1(not_ENA_I), .pin2(INT_MASK_pin9), .pin3(KEYB_INT), .pin4(1'b1), .pin5(keyb_timer_pin5),
    .pin6(keyb_timer_pin6), .pin7(1'b0), .pin8(keyb_timer_pin8), .pin9(keyb_timer_pin9), .pin10(1'b1),
    .pin11(Int_NE555), .pin12(INT_MASK_pin6), .pin13(not_ENA_I), .pin14(1'b1));
  _7410 _7410_1 (
    .pin1(keyb_timer_pin6), .pin2(_7410_1_pin2), .pin3(I_pin5), .pin4(I_pin9), .pin5(CHKI),
    .pin6(_7410_1_pin6), .pin7(1'b0), .pin8(_7410_1_pin8), .pin9(keyb_timer_pin8), .pin10(_7410_1_pin10),
    .pin11(_7410_1_pin11), .pin12(I_pin11), .pin13(1'b1), .pin14(1'b1));
  PullDown pulldown_1 (.out(INT1));
  PullDown pulldown_2 (.out(INT2));
  _74245 _74245_5 (
    .pin1(1'b1), .pin2(_74138_5_pin15), .pin3(_74138_5_pin14), .pin4(_74138_5_pin13), .pin5(_74138_5_pin12),
    .pin6(_74138_5_pin11), .pin7(_74138_5_pin10), .pin8(_74138_5_pin9), .pin9(_74138_5_pin7), .pin10(1'b0),
    .pin11(COL7), .pin12(COL6), .pin13(COL5), .pin14(COL4), .pin15(COL3), .pin16(COL2), .pin17(COL1),
    .pin18(COL0), .pin19(_7400_11_pin8), .pin20(1'b1));
  _74125 _74125_1 (
    .pin1(COL0), .pin2(1'b0), .pin3(switchdt_6_p1), .pin4(COL1), .pin5(1'b0), .pin6(switchdt_14_p1),
    .pin7(1'b0), .pin8(switchdt_22_p1), .pin9(1'b0), .pin10(COL2), .pin11(switchdt_30_p1), .pin12(1'b0),
    .pin13(COL3), .pin14(1'b1));
  _74125 _74125_2 (
    .pin1(COL4), .pin2(1'b0), .pin3(switchdt_38_p1), .pin4(COL5), .pin5(1'b0), .pin6(switchdt_46_p1),
    .pin7(1'b0), .pin8(switchdt_54_p1), .pin9(1'b0), .pin10(COL6), .pin11(switchdt_62_p1), .pin12(1'b0),
    .pin13(COL7), .pin14(1'b1));
  _74161 _74161_1 (
    .pin1(not_CLR), .pin2(Enable_next_IR), .pin3(Data[0]), .pin4(Data[1]), .pin5(Data[2]), .pin6(Data[3]),
    .pin7(CPC), .pin8(1'b0), .pin9(_7400_12_pin6), .pin10(1'b1), .pin11(_74161_1_pin14[3]),
    .pin12(_74161_1_pin14[2]), .pin13(_74161_1_pin14[1]), .pin14(_74161_1_pin14[0]), .pin15(_74161_1_pin15),
    .pin16(1'b1));
  _74161 _74161_2 (
    .pin1(not_CLR), .pin2(Enable_next_IR), .pin3(Data[4]), .pin4(Data[5]), .pin5(Data[6]), .pin6(Data[7]),
    .pin7(CPC), .pin8(1'b0), .pin9(_7400_12_pin6), .pin10(_74161_1_pin15), .pin11(_74161_2_pin14[3]),
    .pin12(_74161_2_pin14[2]), .pin13(_74161_2_pin14[1]), .pin14(_74161_2_pin14[0]), .pin15(_74161_2_pin15),
    .pin16(1'b1));
  _74161 _74161_3 (
    .pin1(not_CLR), .pin2(Enable_next_IR), .pin3(Data[0]), .pin4(Data[1]), .pin5(Data[2]), .pin6(Data[3]),
    .pin7(CPC), .pin8(1'b0), .pin9(_7400_13_pin6), .pin10(_74161_2_pin15), .pin11(_74161_3_pin14[3]),
    .pin12(_74161_3_pin14[2]), .pin13(_74161_3_pin14[1]), .pin14(_74161_3_pin14[0]), .pin15(_74161_3_pin15),
    .pin16(1'b1));
  _74161 _74161_4 (
    .pin1(not_CLR), .pin2(Enable_next_IR), .pin3(Data[4]), .pin4(Data[5]), .pin5(Data[6]), .pin6(Data[7]),
    .pin7(CPC), .pin8(1'b0), .pin9(_7400_13_pin6), .pin10(_74161_3_pin15), .pin11(_74161_4_pin14[3]),
    .pin12(_74161_4_pin14[2]), .pin13(_74161_4_pin14[1]), .pin14(_74161_4_pin14[0]), .pin15(_74161_4_pin15),
    .pin16(1'b1));
  _74161 _74161_5 (
    .pin1(_7408_6_pin11), .pin2(Enable_next_IR), .pin3(Data[0]), .pin4(Data[1]), .pin5(Data[2]),
    .pin6(Data[3]), .pin7(CPC), .pin8(1'b0), .pin9(_7400_13_pin8), .pin10(_74161_4_pin15),
    .pin11(_74161_5_pin14[3]), .pin12(_74161_5_pin14[2]), .pin13(_74161_5_pin14[1]),
    .pin14(_74161_5_pin14[0]), .pin15(_74161_5_pin15), .pin16(1'b1));
  _74161 _74161_6 (
    .pin1(_7408_6_pin11), .pin2(Enable_next_IR), .pin3(Data[4]), .pin4(Data[5]), .pin5(Data[6]),
    .pin6(Data[7]), .pin7(CPC), .pin8(1'b0), .pin9(_7400_13_pin8), .pin10(_74161_5_pin15),
    .pin11(_74161_6_pin14[3]), .pin12(_74161_6_pin14[2]), .pin13(_74161_6_pin14[1]),
    .pin14(_74161_6_pin14[0]), .pin16(1'b1));  // open: pin15
  _7400 _7400_15 (
    .pin1(_7410_1_pin6), .pin2(_7410_1_pin6), .pin3(_7400_15_pin3), .pin4(_7410_1_pin8), .pin5(_7410_1_pin8),
    .pin6(_7410_1_pin2), .pin7(1'b0), .pin8(_7400_15_pin8), .pin9(EEPROM_ready), .pin10(EINT_OUT),
    .pin11(Reset_IRs), .pin12(CLK), .pin13(_7400_15_pin3), .pin14(1'b1));
  _7474 ext_I1_I2 (
    .pin1(not_ENA_I), .pin2(INT_MASK_pin2), .pin3(INT1), .pin4(1'b1), .pin5(ext_I1_I2_pin5),
    .pin6(_7410_1_pin11), .pin7(1'b0), .pin8(_7410_1_pin10), .pin9(ext_I1_I2_pin9), .pin10(1'b1),
    .pin11(INT2), .pin12(INT_MASK_pin5), .pin13(not_ENA_I), .pin14(1'b1));
  _74245 _74245_6 (
    .pin1(1'b1), .pin2(_74138_6_pin15), .pin3(_74138_6_pin14), .pin4(_74138_6_pin13), .pin5(_74138_6_pin12),
    .pin6(_74138_6_pin11), .pin7(_74138_6_pin10), .pin8(_74138_6_pin9), .pin9(_74138_6_pin7), .pin10(1'b0),
    .pin11(COL7), .pin12(COL6), .pin13(COL5), .pin14(COL4), .pin15(COL3), .pin16(COL2), .pin17(COL1),
    .pin18(COL0), .pin19(_74163_1_pin7), .pin20(1'b1));
  _74373 Y (
    .pin1(not_EY), .pin2(Data[0]), .pin3(Data[0]), .pin4(Data[1]), .pin5(Data[1]), .pin6(Data[2]),
    .pin7(Data[2]), .pin8(Data[3]), .pin9(Data[3]), .pin10(1'b0), .pin11(LY), .pin12(Data[4]),
    .pin13(Data[4]), .pin14(Data[5]), .pin15(Data[5]), .pin16(Data[6]), .pin17(Data[6]), .pin18(Data[7]),
    .pin19(Data[7]), .pin20(1'b1));
  _74245 INT_OUT (
    .pin1(1'b1), .pin2(ext_I1_I2_pin5), .pin3(ext_I1_I2_pin9), .pin4(keyb_timer_pin9),
    .pin5(keyb_timer_pin5), .pin6(1'b1), .pin7(1'b1), .pin8(1'b1), .pin9(1'b1), .pin10(1'b0),
    .pin11(Data[7]), .pin12(Data[6]), .pin13(Data[5]), .pin14(Data[4]), .pin15(Data[3]), .pin16(Data[2]),
    .pin17(Data[1]), .pin18(Data[0]), .pin19(_7400_15_pin8), .pin20(1'b1));
  _74163 IC_L (
    .pin1(Reset_T), .pin2(Enable_next_IR), .pin3(1'b0), .pin4(1'b0), .pin5(1'b0), .pin6(1'b0), .pin7(1'b1),
    .pin8(1'b0), .pin9(not_JMP), .pin10(1'b1), .pin11(Ctrl[3]), .pin12(Ctrl[2]), .pin13(Ctrl[1]),
    .pin14(Ctrl[0]), .pin15(IC_L_pin15), .pin16(1'b1));
  _74163 IC_H (
    .pin1(Reset_T), .pin2(Enable_next_IR), .pin3(1'b1), .pin4(1'b0), .pin5(1'b0), .pin6(1'b0), .pin7(1'b1),
    .pin8(1'b0), .pin9(not_JMP), .pin10(IC_L_pin15), .pin14(Ctrl[4]), .pin16(1'b1));  // open: pin11, pin12, pin13, pin15
  _74245 _74245_7 (
    .pin1(1'b1), .pin2(_74161_1_pin14[0]), .pin3(_74161_1_pin14[1]), .pin4(_74161_1_pin14[2]),
    .pin5(_74161_1_pin14[3]), .pin6(_74161_2_pin14[0]), .pin7(_74161_2_pin14[1]), .pin8(_74161_2_pin14[2]),
    .pin9(_74161_2_pin14[3]), .pin10(1'b0), .pin11(Data[7]), .pin12(Data[6]), .pin13(Data[5]),
    .pin14(Data[4]), .pin15(Data[3]), .pin16(Data[2]), .pin17(Data[1]), .pin18(Data[0]), .pin19(not_EPC_L),
    .pin20(1'b1));
  _74245 _74245_8 (
    .pin1(1'b1), .pin2(_74161_3_pin14[0]), .pin3(_74161_3_pin14[1]), .pin4(_74161_3_pin14[2]),
    .pin5(_74161_3_pin14[3]), .pin6(_74161_4_pin14[0]), .pin7(_74161_4_pin14[1]), .pin8(_74161_4_pin14[2]),
    .pin9(_74161_4_pin14[3]), .pin10(1'b0), .pin11(Data[7]), .pin12(Data[6]), .pin13(Data[5]),
    .pin14(Data[4]), .pin15(Data[3]), .pin16(Data[2]), .pin17(Data[1]), .pin18(Data[0]), .pin19(not_EPC_H),
    .pin20(1'b1));
  _74245 _74245_9 (
    .pin1(1'b1), .pin2(_74161_5_pin14[0]), .pin3(_74161_5_pin14[1]), .pin4(_74161_5_pin14[2]),
    .pin5(_74161_5_pin14[3]), .pin6(_74161_6_pin14[0]), .pin7(_74161_6_pin14[1]), .pin8(_74161_6_pin14[2]),
    .pin9(_74161_6_pin14[3]), .pin10(1'b0), .pin11(Data[7]), .pin12(Data[6]), .pin13(Data[5]),
    .pin14(Data[4]), .pin15(Data[3]), .pin16(Data[2]), .pin17(Data[1]), .pin18(Data[0]),
    .pin19(not_EPC_PAGE), .pin20(1'b1));
  _74373 TMP (
    .pin1(not_ETMP), .pin2(Data[0]), .pin3(Data[0]), .pin4(Data[1]), .pin5(Data[1]), .pin6(Data[2]),
    .pin7(Data[2]), .pin8(Data[3]), .pin9(Data[3]), .pin10(1'b0), .pin11(LTMP), .pin12(Data[4]),
    .pin13(Data[4]), .pin14(Data[5]), .pin15(Data[5]), .pin16(Data[6]), .pin17(Data[6]), .pin18(Data[7]),
    .pin19(Data[7]), .pin20(1'b1));
  PullUp pullup_7 (.out(ROW0));
  PullUp pullup_8 (.out(ROW1));
  PullUp pullup_9 (.out(ROW2));
  PullUp pullup_10 (.out(ROW3));
  PullUp pullup_11 (.out(ROW4));
  PullUp pullup_12 (.out(ROW5));
  PullUp pullup_13 (.out(ROW6));
  PullUp pullup_14 (.out(ROW7));
  _74245 _74245_10 (
    .pin1(1'b1), .pin2(_74161_1_pin14[0]), .pin3(_74161_1_pin14[1]), .pin4(_74161_1_pin14[2]),
    .pin5(_74161_1_pin14[3]), .pin6(_74161_2_pin14[0]), .pin7(_74161_2_pin14[1]), .pin8(_74161_2_pin14[2]),
    .pin9(_74161_2_pin14[3]), .pin10(1'b0), .pin11(Addr[7]), .pin12(Addr[6]), .pin13(Addr[5]),
    .pin14(Addr[4]), .pin15(Addr[3]), .pin16(Addr[2]), .pin17(Addr[1]), .pin18(Addr[0]),
    .pin19(_7400_12_pin8), .pin20(1'b1));
  _74245 _74245_11 (
    .pin1(1'b1), .pin2(_74161_3_pin14[0]), .pin3(_74161_3_pin14[1]), .pin4(_74161_3_pin14[2]),
    .pin5(_74161_3_pin14[3]), .pin6(_74161_4_pin14[0]), .pin7(_74161_4_pin14[1]), .pin8(_74161_4_pin14[2]),
    .pin9(_74161_4_pin14[3]), .pin10(1'b0), .pin11(Addr[15]), .pin12(Addr[14]), .pin13(Addr[13]),
    .pin14(Addr[12]), .pin15(Addr[11]), .pin16(Addr[10]), .pin17(Addr[9]), .pin18(Addr[8]),
    .pin19(_7400_12_pin8), .pin20(1'b1));
  _74245 _74245_12 (
    .pin1(1'b1), .pin2(_74161_5_pin14[0]), .pin3(_74161_5_pin14[1]), .pin4(_74161_5_pin14[2]),
    .pin5(_74161_5_pin14[3]), .pin6(_74161_6_pin14[0]), .pin7(_74161_6_pin14[1]), .pin8(_74161_6_pin14[2]),
    .pin9(_74161_6_pin14[3]), .pin10(1'b0), .pin11(Addr[23]), .pin12(Addr[22]), .pin13(Addr[21]),
    .pin14(Addr[20]), .pin15(Addr[19]), .pin16(Addr[18]), .pin17(Addr[17]), .pin18(Addr[16]),
    .pin19(_7400_12_pin8), .pin20(1'b1));
  _74373 D (
    .pin1(not_ED), .pin2(Data[0]), .pin3(Data[0]), .pin4(Data[1]), .pin5(Data[1]), .pin6(Data[2]),
    .pin7(Data[2]), .pin8(Data[3]), .pin9(Data[3]), .pin10(1'b0), .pin11(LD), .pin12(Data[4]),
    .pin13(Data[4]), .pin14(Data[5]), .pin15(Data[5]), .pin16(Data[6]), .pin17(Data[6]), .pin18(Data[7]),
    .pin19(Data[7]), .pin20(1'b1));
  _74273 Next_IR (
    .pin1(Reset_IRs), .pin2(Next_IR_pin2), .pin3(Data[0]), .pin4(Data[1]), .pin5(Next_IR_pin5),
    .pin6(Next_IR_pin6), .pin7(Data[2]), .pin8(Data[3]), .pin9(Next_IR_pin9), .pin10(1'b0),
    .pin11(Load_next_IR), .pin12(Next_IR_pin12), .pin13(Data[4]), .pin14(Data[5]), .pin15(Next_IR_pin15),
    .pin16(Next_IR_pin16), .pin17(Data[6]), .pin18(Data[7]), .pin19(Next_IR_pin19), .pin20(1'b1));
  _74540 _74540_1 (
    .pin1(1'b0), .pin2(ROW0), .pin3(ROW1), .pin4(ROW2), .pin5(ROW3), .pin6(ROW4), .pin7(ROW5), .pin8(ROW6),
    .pin9(ROW7), .pin10(1'b0), .pin11(_74540_1_pin11), .pin12(_74540_1_pin12), .pin13(_74540_1_pin13),
    .pin14(_74540_1_pin14), .pin15(_74540_1_pin15), .pin16(_74540_1_pin16), .pin17(_74540_1_pin17),
    .pin18(_74540_1_pin18), .pin19(1'b0), .pin20(1'b1));
  _74373 E (
    .pin1(not_EE), .pin2(Data[0]), .pin3(Data[0]), .pin4(Data[1]), .pin5(Data[1]), .pin6(Data[2]),
    .pin7(Data[2]), .pin8(Data[3]), .pin9(Data[3]), .pin10(1'b0), .pin11(LE), .pin12(Data[4]),
    .pin13(Data[4]), .pin14(Data[5]), .pin15(Data[5]), .pin16(Data[6]), .pin17(Data[6]), .pin18(Data[7]),
    .pin19(Data[7]), .pin20(1'b1));
  _74273 IR (
    .pin1(1'b1), .pin2(Ctrl[8]), .pin3(Next_IR_pin2), .pin4(Next_IR_pin5), .pin5(Ctrl[9]), .pin6(Ctrl[10]),
    .pin7(Next_IR_pin6), .pin8(Next_IR_pin9), .pin9(Ctrl[11]), .pin10(1'b0), .pin11(Enable_next_IR),
    .pin12(Ctrl[12]), .pin13(Next_IR_pin12), .pin14(Next_IR_pin15), .pin15(Ctrl[13]), .pin16(Ctrl[14]),
    .pin17(Next_IR_pin16), .pin18(Next_IR_pin19), .pin19(Ctrl[15]), .pin20(1'b1));
  _74245 _74245_13 (
    .pin1(1'b1), .pin2(_74540_1_pin18), .pin3(_74540_1_pin17), .pin4(_74540_1_pin16), .pin5(_74540_1_pin15),
    .pin6(_74540_1_pin14), .pin7(_74540_1_pin13), .pin8(_74540_1_pin12), .pin9(_74540_1_pin11), .pin10(1'b0),
    .pin11(Data[7]), .pin12(Data[6]), .pin13(Data[5]), .pin14(Data[4]), .pin15(Data[3]), .pin16(Data[2]),
    .pin17(Data[1]), .pin18(Data[0]), .pin19(_74163_1_pin7), .pin20(1'b1));
  _74688 _74688_1 (
    .pin1(1'b0), .pin2(_74540_1_pin18), .pin3(_74688_1_pin3), .pin4(_74540_1_pin17), .pin5(_74688_1_pin5),
    .pin6(_74540_1_pin16), .pin7(_74688_1_pin7), .pin8(_74540_1_pin15), .pin9(_74688_1_pin9), .pin10(1'b0),
    .pin11(_74540_1_pin14), .pin12(_74688_1_pin12), .pin13(_74540_1_pin13), .pin14(_74688_1_pin14),
    .pin15(_74540_1_pin12), .pin16(_74688_1_pin16), .pin17(_74540_1_pin11), .pin18(_74688_1_pin18),
    .pin19(_7400_10_pin1), .pin20(1'b1));
  _74189 _74189_1 (
    .pin1(_74163_2_pin14), .pin2(1'b0), .pin3(_74138_4_pin12), .pin4(ROW0), .pin5(_74688_1_pin3),
    .pin6(ROW1), .pin7(_74688_1_pin5), .pin8(1'b0), .pin9(_74688_1_pin7), .pin10(ROW2),
    .pin11(_74688_1_pin9), .pin12(ROW3), .pin13(XOR_pin11), .pin14(_74163_2_pin12), .pin15(_74163_2_pin13),
    .pin16(1'b1));
  _74189 _74189_2 (
    .pin1(_74163_2_pin14), .pin2(1'b0), .pin3(_74138_4_pin12), .pin4(ROW4), .pin5(_74688_1_pin12),
    .pin6(ROW5), .pin7(_74688_1_pin14), .pin8(1'b0), .pin9(_74688_1_pin16), .pin10(ROW6),
    .pin11(_74688_1_pin18), .pin12(ROW7), .pin13(XOR_pin11), .pin14(_74163_2_pin12), .pin15(_74163_2_pin13),
    .pin16(1'b1));
  _74373 OUT (
    .pin1(1'b0), .pin2(OUT_pin2[0]), .pin3(Data[0]), .pin4(Data[1]), .pin5(OUT_pin2[1]), .pin6(OUT_pin2[2]),
    .pin7(Data[2]), .pin8(Data[3]), .pin9(OUT_pin2[3]), .pin10(1'b0), .pin11(LOUT), .pin12(OUT_pin12[0]),
    .pin13(Data[4]), .pin14(Data[5]), .pin15(OUT_pin12[1]), .pin16(OUT_pin12[2]), .pin17(Data[6]),
    .pin18(Data[7]), .pin19(OUT_pin12[3]), .pin20(1'b1));

  assign CLK_2 = CLK;
  assign Ctrl[7:5] = 3'b000;
  assign Inc_T = Enable_next_IR;
  assign not_CLK = Enable_next_IR;
  assign not_CLK_2 = Enable_next_IR;
  assign not_CLR_2 = not_CLR;
  assign not_HLT_2 = not_HLT;

  // Notes on the sheet:
  //   NE555___ext_CLK__to_do: Hz: 1000
  //   Int_NE555: Hz: 10
  //   clk_3: Hz: 1920
  //   EEPROM ready
  //   CLK
  //   not JMP
  //   Memory Page Zero
  //   not Memory WRITE / READ (output)
  //   not Memory ADDR Valid (output)
  //   not Memory Write / Read
  //   not Memory ADDR valid
  //   Data Bus
  //   Address Bus
  //   Address Bus (write)
  //   Address Bus (read)
  //   Control Bus (IC + t)
  //   Control Bus
  //   Clock & Ctrl board
  //   Registers board
  //   Instructions board
  //   CLEAR (push)
  //   STEP (push)
  //   MANUAL/AUTO (switch)
  //   PC/SP board
  //   Keyboard board
  //   Check if read (LDA)
  //   If STA, ignored
  //   Check if zero page
  //   ext INT 1
  //   not CLR
  //   not HLT
  //   not CLK
  //   TODO: allow SP relocation?
  //   Need to change higher 8 bit from 0xFF 
  //   to anything else?
  //   Can we read/write SP replacing 74245 with register?
  //   ext INT 2
  //   Address comparison - in real PCB add
  //   a dip switch to configure it
  //   PC
  //   CLK/2
  //   EEPROM ready is activated 1/4 of cycle after CLK falling.
  //   Use this signal to react and avoid eeprom glitch
  //   Registry output is activated on EEPROM ready signal
  //   Registry load is activated later, on CLK rising up
  //   SP
  //   Enable interrupt 
  //   on CLI
  //   Out
  //   Disable interrupt
  //   on SEI or CLR
  //   CHKI & INT Enabled 
  //   & INT value
  //   (nand)
  //   To avoid conflicts on power up, the OE is inverted.
  //   (on power up exit of buffer is 0)
  //   Output is enabled on eeprom ready only
  //   IC reset (SR) is activated on NOP or CLR (go to T=0)
  //   IC preset (PE) is activated on JMP signal to 
  //   jump to second part of uCode (go to T=16)
  //   IC inc (CP) is activated by falling CLK
  //   Generate control bus
  //   Both IRs are set 
  //   to 0x00 when 
  //   INT must be
  //   handled
  //   Next IR is loaded on 
  //   rising CLK
  //   Value loaded in Next IR is 
  //   presented to control bus 
  //   by IR on falling CLK
  //   contents of Control Word #3 (hex, n*v repeats v):
  //   /Users/Vittorio.Nardone/Documents/__private__/sap-project/roms/cw3-rom.hex false
  //   contents of Registers Control Word (hex, n*v repeats v):
  //   /Users/Vittorio.Nardone/Documents/__private__/sap-project/roms/cw7-rom.hex false
  //   contents of Control Word #2 (hex, n*v repeats v):
  //   /Users/Vittorio.Nardone/Documents/__private__/sap-project/roms/cw2-rom.hex false
  //   contents of PC/SP Control Word (hex, n*v repeats v):
  //   /Users/Vittorio.Nardone/Documents/__private__/sap-project/roms/cw9-rom.hex false
  //   contents of Control Word #6 (hex, n*v repeats v):
  //   /Users/Vittorio.Nardone/Documents/__private__/sap-project/roms/cw6-rom.hex false
  //   contents of Control Word #5 (hex, n*v repeats v):
  //   /Users/Vittorio.Nardone/Documents/__private__/sap-project/roms/cw5-rom.hex false
  //   contents of Control Word #4 (hex, n*v repeats v):
  //   /Users/Vittorio.Nardone/Documents/__private__/sap-project/roms/cw4-rom.hex false
  //   contents of Memory Control Word (hex, n*v repeats v):
  //   /Users/Vittorio.Nardone/Documents/__private__/sap-project/roms/cw1-rom.hex false
  //   contents of Instructions Control Word (hex, n*v repeats v):
  //   /Users/Vittorio.Nardone/Documents/__private__/sap-project/roms/cw8-rom.hex false
  //   contents of ROM (1st 8k) (hex, n*v repeats v):
  //   /Users/Vittorio.Nardone/Documents/__private__/sap-project/roms/kernel-rom.hex false
endmodule
