// Digital circuit simulation.dig as structural Verilog
module simulation (
  input  NE555___ext_CLK__to_do,
  input  Int_NE555,
  output not_CLR,
  output CLK,
  output not_CLK,
  output CPC,
  output a0,
  output not_ERAM,
  output not_EPC_RAM,
  output a7,
  output a4,
  output a5,
  output HLT,
  output LMAR_L,
  output LMAR_H,
  output not_EMAR,
  output not_WRAM,
  output not_LPC_H,
  output not_LPC_L,
  output LRALU_IN,
  output LRALU_OUT,
  output ALUS0,
  output ALUS1,
  output ALUS2,
  output ALUS3,
  output ALUCN,
  output ALUM,
  output not_ERALU_OUT,
  output a7_2,
  output a0_2,
  output a1,
  output a2,
  output a3,
  output LC,
  output CHKZ,
  output CHKC,
  output not_CLC,
  output not_SEC,
  output LZ,
  output not_CSP,
  output SPD,
  output not_ESP,
  output not_EPC_L,
  output not_EPC_H,
  output a7_3,
  output a0_3,
  output a1_2,
  output a2_2,
  output a3_2,
  output LO,
  output CHKO,
  output not_EFR_out,
  output EFR_in,
  output not_CLR_2,
  output not_HLT,
  output CLK_2,
  output not_CLK_2,
  output CLR__not_used,
  output EEPROM_ready,
  output LPCH_Load,
  output not_JMP,
  output LIR,
  output CHKI,
  output not_HLT_2,
  output not_ENA_I,
  output not_DIS_I,
  output not_NOP,
  output out_67,
  output not_EINT_OUT,
  output Reset_IR,
  output Load_IR,
  output Inc_T,
  output Reset_T,
  output INT1,
  output INT2
);

  wire _7400_1_pin5, _7400_1_pin8, _7400_1_pin10, _7400_1_pin11, _7400_1_pin12, _7400_2_pin6, _7400_2_pin10,
       _7400_3_pin3, _7404_1_pin9, _7404_2_pin12, _7408_1_pin1, _7408_1_pin2, _7408_1_pin6, _7408_2_pin6,
       _7408_2_pin9, _7408_2_pin10, _7408_2_pin11, _7408_3_pin3, _7408_3_pin5, _7408_3_pin10, _7410_1_pin6,
       _7410_1_pin10, _7410_1_pin11, _7432_1_pin9, _7432_1_pin10, _74138_1_pin1, _74138_1_pin2,
       _74138_1_pin3, _74138_1_pin9, _74138_1_pin10, _74138_1_pin11, _74138_1_pin12, _74138_1_pin13,
       _74138_1_pin14, _74161_1_pin15, _74161_2_pin15, _74161_3_pin15, _74191_1_pin13, _74238_1_pin7,
       _74238_1_pin9, _74238_1_pin10, _74238_1_pin11, _74238_1_pin12, _74238_1_pin13, _74238_1_pin14,
       _74373_1_pin8, _74373_1_pin13, _74373_1_pin14, _74373_1_pin17, ALU_H_pin2, ALU_H_pin7, ALU_H_pin9,
       ALU_H_pin10, ALU_H_pin11, ALU_L_pin2, ALU_L_pin9, ALU_L_pin10, ALU_L_pin11, and_1_out, and_2_out,
       bussplitter_3_d0, bussplitter_3_d1, bussplitter_3_d2, bussplitter_3_d3, bussplitter_3_d4,
       bussplitter_3_d5, bussplitter_3_d6, bussplitter_3_d7, CLOCK_BUF_pin2, CLOCK_BUF_pin11,
       CLOCK_BUF_pin13, Debouncer_2_pin2, Debouncer_2_pin3, Debouncer_2_pin8, Debouncer_2_pin10,
       Debouncer_2_pin11, Debouncer_2_pin12, Debouncer_pin8, Debouncer_pin10, ext_I_pin5, ext_I_pin9,
       FR_in_pin9, FR_in_pin11, FR_in_pin12, FR_in_pin14, I_pin5, I_pin9, I_pin11, IC_L_pin15,
       Instructions_Control_Word_p17, Instructions_Control_Word_p19, Instructions_Control_Word_p20,
       Instructions_Control_Word_p21, MAR_H_pin2, MAR_H_pin5, MAR_H_pin6, MAR_H_pin9, MAR_H_pin12,
       MAR_H_pin15, MAR_H_pin16, MAR_H_pin19, MAR_L_pin2, MAR_L_pin5, MAR_L_pin6, MAR_L_pin9, MAR_L_pin12,
       MAR_L_pin15, MAR_L_pin16, MAR_L_pin19, not_1_out, not_2_out, RALU_IN_pin5, RALU_IN_pin6, RALU_IN_pin9,
       RALU_IN_pin15, RALU_IN_pin16, RALU_IN_pin19, RALU_OUT_pin8, RALU_OUT_pin18,
       Registers_Control_Word_p18, Registers_Control_Word_p19, Registers_Control_Word_p20, switchdt_1_p2,
       switchdt_1_p3, switchdt_2_p2, switchdt_2_p3, switchdt_3_p2, switchdt_3_p3;
  wire [3:0] _74161_1_pin14, _74161_2_pin14, _74161_3_pin14, _74161_4_pin14, _74245_6_pin5, _74245_6_pin9,
       Control_Word__6_p15, Control_Word__6_p16, FR_OUT_pin14, FR_OUT_pin18, OUT_pin2, OUT_pin12;
  wire [4:0] Control_Word__6_p5;
  wire [7:0] bussplitter_1_d;
  wire [15:0] bussplitter_2_d;

  // _28c64 Control_Word__6: pin names not known; wires that end beside it: 1'b0, a2_2, a1_2, a0_3, Control_Word__6_p5[0], EFR_in, Control_Word__6_p5[1], 1'b0, Control_Word__6_p5[2], Control_Word__6_p16[1], Control_Word__6_p5[3], 1'b0, Control_Word__6_p5[4], Control_Word__6_p16[2], Control_Word__6_p15[0], Control_Word__6_p16[0], Control_Word__6_p15[1], Control_Word__6_p15[3], Control_Word__6_p15[2], Control_Word__6_p16[3], 1'b1, 1'b1
  // _28c64 Control_Word__5: pin names not known; wires that end beside it: 1'b0, not_CSP, LZ, not_SEC, Control_Word__6_p5[0], a7_3, Control_Word__6_p5[1], 1'b0, Control_Word__6_p5[2], Control_Word__6_p16[1], Control_Word__6_p5[3], 1'b0, Control_Word__6_p5[4], Control_Word__6_p16[2], Control_Word__6_p15[0], Control_Word__6_p16[0], Control_Word__6_p15[1], Control_Word__6_p15[3], Control_Word__6_p15[2], Control_Word__6_p16[3], 1'b1, 1'b1
  _7408 _7408_1 (
    .pin1(_7408_1_pin1), .pin2(_7408_1_pin2), .pin3(not_JMP), .pin4(CLK), .pin5(LO), .pin6(_7408_1_pin6),
    .pin7(1'b0), .pin9(1'b1), .pin10(1'b1), .pin12(1'b1), .pin13(1'b1), .pin14(1'b1));  // open: pin8, pin11
  // _28c64 Control_Word__4: pin names not known; wires that end beside it: 1'b0, a2, a1, a0_2, Control_Word__6_p5[0], not_CLC, Control_Word__6_p5[1], 1'b0, Control_Word__6_p5[2], Control_Word__6_p16[1], Control_Word__6_p5[3], 1'b0, Control_Word__6_p5[4], Control_Word__6_p16[2], Control_Word__6_p15[0], Control_Word__6_p16[0], Control_Word__6_p15[1], Control_Word__6_p15[3], Control_Word__6_p15[2], Control_Word__6_p16[3], 1'b1, 1'b1
  _74157 FR_in (
    .pin1(EFR_in), .pin2(1'b1), .pin3(1'b1), .pin5(1'b1), .pin6(1'b1), .pin8(1'b0), .pin9(FR_in_pin9),
    .pin10(FR_OUT_pin18[2]), .pin11(FR_in_pin11), .pin12(FR_in_pin12), .pin13(FR_OUT_pin18[3]),
    .pin14(FR_in_pin14), .pin15(1'b0), .pin16(1'b1));  // open: pin4, pin7
  _7400 _7400_1 (
    .pin1(1'b0), .pin2(1'b0), .pin4(CHKO), .pin5(_7400_1_pin5), .pin6(_7408_1_pin2), .pin7(1'b0),
    .pin8(_7400_1_pin8), .pin9(CHKC), .pin10(_7400_1_pin10), .pin11(_7400_1_pin11), .pin12(_7400_1_pin12),
    .pin13(CHKZ), .pin14(1'b1));  // open: pin3
  _7432 _7432_1 (
    .pin1(1'b0), .pin2(1'b0), .pin4(1'b0), .pin5(1'b0), .pin7(1'b0), .pin8(FR_in_pin14), .pin9(_7432_1_pin9),
    .pin10(_7432_1_pin10), .pin12(1'b1), .pin13(1'b1), .pin14(1'b1));  // open: pin3, pin6, pin11
  _7474 O (
    .pin1(1'b1), .pin2(1'b1), .pin3(1'b0), .pin4(1'b1), .pin7(1'b0), .pin8(_7400_1_pin5), .pin10(1'b1),
    .pin11(_7408_1_pin6), .pin12(FR_in_pin11), .pin13(1'b1), .pin14(1'b1));  // open: pin5, pin6, pin9
  _74245 FR_OUT (
    .pin1(1'b1), .pin2(1'b1), .pin3(1'b1), .pin4(_7400_1_pin10), .pin5(_7400_1_pin12), .pin6(1'b1),
    .pin7(1'b1), .pin8(1'b1), .pin9(1'b1), .pin10(1'b0), .pin11(FR_OUT_pin14[3]), .pin12(FR_OUT_pin14[2]),
    .pin13(FR_OUT_pin14[1]), .pin14(FR_OUT_pin14[0]), .pin15(FR_OUT_pin18[3]), .pin16(FR_OUT_pin18[2]),
    .pin17(FR_OUT_pin18[1]), .pin18(FR_OUT_pin18[0]), .pin19(not_EFR_out), .pin20(1'b1));
  Seven_Seg_Hex seven_seg_hex_1 (.d(FR_OUT_pin14), .dp(1'b0));
  Seven_Seg_Hex seven_seg_hex_2 (.d(FR_OUT_pin18), .dp(1'b0));
  _7408 _7408_2 (
    .pin1(_7400_1_pin11), .pin2(_7400_1_pin8), .pin3(_7408_1_pin1), .pin4(CLK), .pin5(LZ),
    .pin6(_7408_2_pin6), .pin7(1'b0), .pin8(_7432_1_pin9), .pin9(_7408_2_pin9), .pin10(_7408_2_pin10),
    .pin11(_7408_2_pin11), .pin12(CLK), .pin13(LC), .pin14(1'b1));
  _7474 Z___C (
    .pin1(1'b1), .pin2(FR_in_pin12), .pin3(_7408_2_pin6), .pin4(1'b1), .pin5(_7400_1_pin12), .pin7(1'b0),
    .pin9(_7400_1_pin10), .pin10(not_SEC), .pin11(_7408_2_pin11), .pin12(FR_in_pin9), .pin13(not_CLC),
    .pin14(1'b1));  // open: pin6, pin8
  // _28c64 Control_Word__3: pin names not known; wires that end beside it: 1'b0, ALUS2, ALUS1, ALUS0, Control_Word__6_p5[0], a7_2, Control_Word__6_p5[1], 1'b0, Control_Word__6_p5[2], Control_Word__6_p16[1], Control_Word__6_p5[3], 1'b0, Control_Word__6_p5[4], Control_Word__6_p16[2], Control_Word__6_p15[0], Control_Word__6_p16[0], Control_Word__6_p15[1], Control_Word__6_p15[3], Control_Word__6_p15[2], Control_Word__6_p16[3], 1'b1, 1'b1, 1'b0
  Seven_Seg_Hex seven_seg_hex_3 (.d(_74161_4_pin14), .dp(1'b0));
  Seven_Seg_Hex seven_seg_hex_4 (.d(_74161_3_pin14), .dp(1'b0));
  Seven_Seg_Hex seven_seg_hex_5 (.d(_74161_2_pin14), .dp(1'b0));
  Seven_Seg_Hex seven_seg_hex_6 (.d(_74161_1_pin14), .dp(1'b0));
  // _28c64 Control_Word__2: pin names not known; wires that end beside it: not_EMAR, LMAR_H, LMAR_L, Control_Word__6_p5[0], LRALU_OUT, Control_Word__6_p5[1], 1'b0, Control_Word__6_p5[2], Control_Word__6_p16[1], Control_Word__6_p5[3], 1'b0, Control_Word__6_p5[4], Control_Word__6_p16[2], Control_Word__6_p15[0], Control_Word__6_p16[0], Control_Word__6_p15[1], Control_Word__6_p15[3], Control_Word__6_p15[2], Control_Word__6_p16[3], 1'b1, 1'b1, 1'b0, not_EPC_RAM
  _74181 ALU_L (
    .pin1(FR_OUT_pin18[0]), .pin2(ALU_L_pin2), .pin3(ALUS3), .pin4(ALUS2), .pin5(ALUS1), .pin6(ALUS0),
    .pin7(ALUCN), .pin8(ALUM), .pin9(ALU_L_pin9), .pin10(ALU_L_pin10), .pin11(ALU_L_pin11), .pin12(1'b0));  // open: pin13, pin14, pin15, pin16, pin17, pin18, pin19, pin20, pin21, pin22, pin23, pin24
  _74181 ALU_H (
    .pin1(FR_OUT_pin14[0]), .pin2(ALU_H_pin2), .pin3(ALUS3), .pin4(ALUS2), .pin5(ALUS1), .pin6(ALUS0),
    .pin7(ALU_H_pin7), .pin8(ALUM), .pin9(ALU_H_pin9), .pin10(ALU_H_pin10), .pin11(ALU_H_pin11), .pin12(1'b0));  // open: pin13, pin14, pin15, pin16, pin17, pin18, pin19, pin20, pin21, pin22, pin23, pin24
  _7404 _7404_1 (
    .pin1(1'b0), .pin3(1'b0), .pin5(1'b0), .pin7(1'b0), .pin8(_7432_1_pin10), .pin9(_7404_1_pin9),
    .pin11(1'b1), .pin13(1'b1), .pin14(1'b1));  // open: pin2, pin4, pin6, pin10, pin12
  _74688 Z_BUS (
    .pin1(1'b0), .pin2(1'b0), .pin3(FR_OUT_pin18[0]), .pin4(1'b0), .pin5(FR_OUT_pin18[1]), .pin6(1'b0),
    .pin7(FR_OUT_pin18[2]), .pin8(1'b0), .pin9(FR_OUT_pin18[3]), .pin10(1'b0), .pin11(1'b0),
    .pin12(FR_OUT_pin14[0]), .pin13(1'b0), .pin14(FR_OUT_pin14[1]), .pin15(1'b0), .pin16(FR_OUT_pin14[2]),
    .pin17(1'b0), .pin18(FR_OUT_pin14[3]), .pin19(_7404_1_pin9), .pin20(1'b1));
  // _28c64 Control_Word__1: pin names not known; wires that end beside it: not_ERAM, a0, Control_Word__6_p5[0], a7, Control_Word__6_p5[1], 1'b0, Control_Word__6_p5[2], Control_Word__6_p16[1], Control_Word__6_p5[3], 1'b0, Control_Word__6_p5[4], Control_Word__6_p16[2], Control_Word__6_p15[0], Control_Word__6_p16[0], Control_Word__6_p15[1], Control_Word__6_p15[3], Control_Word__6_p15[2], Control_Word__6_p16[3], 1'b1, 1'b1
  _74373 RALU_IN (
    .pin1(1'b0), .pin2(ALU_L_pin2), .pin3(FR_OUT_pin18[0]), .pin4(FR_OUT_pin18[1]), .pin5(RALU_IN_pin5),
    .pin6(RALU_IN_pin6), .pin7(FR_OUT_pin18[2]), .pin8(FR_OUT_pin18[3]), .pin9(RALU_IN_pin9), .pin10(1'b0),
    .pin11(LRALU_IN), .pin12(ALU_H_pin2), .pin13(FR_OUT_pin14[0]), .pin14(FR_OUT_pin14[1]),
    .pin15(RALU_IN_pin15), .pin16(RALU_IN_pin16), .pin17(FR_OUT_pin14[2]), .pin18(FR_OUT_pin14[3]),
    .pin19(RALU_IN_pin19), .pin20(1'b1));
  _74373 RALU_OUT (
    .pin1(not_ERALU_OUT), .pin2(FR_OUT_pin18[0]), .pin3(ALU_L_pin9), .pin4(ALU_L_pin10),
    .pin5(FR_OUT_pin18[1]), .pin6(FR_OUT_pin18[2]), .pin7(ALU_L_pin11), .pin8(RALU_OUT_pin8),
    .pin9(FR_OUT_pin18[3]), .pin10(1'b0), .pin11(LRALU_OUT), .pin12(FR_OUT_pin14[0]), .pin13(ALU_H_pin9),
    .pin14(ALU_H_pin10), .pin15(FR_OUT_pin14[1]), .pin16(FR_OUT_pin14[2]), .pin17(ALU_H_pin11),
    .pin18(RALU_OUT_pin18), .pin19(FR_OUT_pin14[3]), .pin20(1'b1));
  BusSplitter #(.Bits(8)) bussplitter_1 (
    .D(bussplitter_1_d), .OE(not_1_out), .D0(FR_OUT_pin18[0]), .D1(FR_OUT_pin18[1]), .D2(FR_OUT_pin18[2]),
    .D3(FR_OUT_pin18[3]), .D4(FR_OUT_pin14[0]), .D5(FR_OUT_pin14[1]), .D6(FR_OUT_pin14[2]),
    .D7(FR_OUT_pin14[3]));
  _74161 _74161_1 (
    .pin1(not_CLR), .pin2(Inc_T), .pin3(FR_OUT_pin18[0]), .pin4(FR_OUT_pin18[1]), .pin5(FR_OUT_pin18[2]),
    .pin6(FR_OUT_pin18[3]), .pin7(CPC), .pin8(1'b0), .pin9(not_LPC_L), .pin10(1'b1),
    .pin11(_74161_1_pin14[3]), .pin12(_74161_1_pin14[2]), .pin13(_74161_1_pin14[1]),
    .pin14(_74161_1_pin14[0]), .pin15(_74161_1_pin15), .pin16(1'b1));
  _74161 _74161_2 (
    .pin1(not_CLR), .pin2(Inc_T), .pin3(FR_OUT_pin14[0]), .pin4(FR_OUT_pin14[1]), .pin5(FR_OUT_pin14[2]),
    .pin6(FR_OUT_pin14[3]), .pin7(CPC), .pin8(1'b0), .pin9(not_LPC_L), .pin10(_74161_1_pin15),
    .pin11(_74161_2_pin14[3]), .pin12(_74161_2_pin14[2]), .pin13(_74161_2_pin14[1]),
    .pin14(_74161_2_pin14[0]), .pin15(_74161_2_pin15), .pin16(1'b1));
  _74161 _74161_3 (
    .pin1(not_CLR), .pin2(Inc_T), .pin3(FR_OUT_pin18[0]), .pin4(FR_OUT_pin18[1]), .pin5(FR_OUT_pin18[2]),
    .pin6(FR_OUT_pin18[3]), .pin7(CPC), .pin8(1'b0), .pin9(LPCH_Load), .pin10(_74161_2_pin15),
    .pin11(_74161_3_pin14[3]), .pin12(_74161_3_pin14[2]), .pin13(_74161_3_pin14[1]),
    .pin14(_74161_3_pin14[0]), .pin15(_74161_3_pin15), .pin16(1'b1));
  _74161 _74161_4 (
    .pin1(not_CLR), .pin2(Inc_T), .pin3(FR_OUT_pin14[0]), .pin4(FR_OUT_pin14[1]), .pin5(FR_OUT_pin14[2]),
    .pin6(FR_OUT_pin14[3]), .pin7(CPC), .pin8(1'b0), .pin9(LPCH_Load), .pin10(_74161_3_pin15),
    .pin11(_74161_4_pin14[3]), .pin12(_74161_4_pin14[2]), .pin13(_74161_4_pin14[1]),
    .pin14(_74161_4_pin14[0]), .pin16(1'b1));  // open: pin15
  _74373 MAR_L (
    .pin1(not_EMAR), .pin2(MAR_L_pin2), .pin3(FR_OUT_pin18[0]), .pin4(FR_OUT_pin18[1]), .pin5(MAR_L_pin5),
    .pin6(MAR_L_pin6), .pin7(FR_OUT_pin18[2]), .pin8(FR_OUT_pin18[3]), .pin9(MAR_L_pin9), .pin10(1'b0),
    .pin11(LMAR_L), .pin12(MAR_L_pin12), .pin13(FR_OUT_pin14[0]), .pin14(FR_OUT_pin14[1]),
    .pin15(MAR_L_pin15), .pin16(MAR_L_pin16), .pin17(FR_OUT_pin14[2]), .pin18(FR_OUT_pin14[3]),
    .pin19(MAR_L_pin19), .pin20(1'b1));
  _74373 MAR_H (
    .pin1(not_EMAR), .pin2(MAR_H_pin2), .pin3(FR_OUT_pin18[0]), .pin4(FR_OUT_pin18[1]), .pin5(MAR_H_pin5),
    .pin6(MAR_H_pin6), .pin7(FR_OUT_pin18[2]), .pin8(FR_OUT_pin18[3]), .pin9(MAR_H_pin9), .pin10(1'b0),
    .pin11(LMAR_H), .pin12(MAR_H_pin12), .pin13(FR_OUT_pin14[0]), .pin14(FR_OUT_pin14[1]),
    .pin15(MAR_H_pin15), .pin16(MAR_H_pin16), .pin17(FR_OUT_pin14[2]), .pin18(FR_OUT_pin14[3]),
    .pin19(MAR_H_pin19), .pin20(1'b1));
  _74245 _74245_1 (
    .pin1(1'b1), .pin2(_74161_1_pin14[0]), .pin3(_74161_1_pin14[1]), .pin4(_74161_1_pin14[2]),
    .pin5(_74161_1_pin14[3]), .pin6(_74161_2_pin14[0]), .pin7(_74161_2_pin14[1]), .pin8(_74161_2_pin14[2]),
    .pin9(_74161_2_pin14[3]), .pin10(1'b0), .pin11(FR_OUT_pin14[3]), .pin12(FR_OUT_pin14[2]),
    .pin13(FR_OUT_pin14[1]), .pin14(FR_OUT_pin14[0]), .pin15(FR_OUT_pin18[3]), .pin16(FR_OUT_pin18[2]),
    .pin17(FR_OUT_pin18[1]), .pin18(FR_OUT_pin18[0]), .pin19(not_EPC_L), .pin20(1'b1));
  _74245 _74245_2 (
    .pin1(1'b1), .pin2(_74161_3_pin14[0]), .pin3(_74161_3_pin14[1]), .pin4(_74161_3_pin14[2]),
    .pin5(_74161_3_pin14[3]), .pin6(_74161_4_pin14[0]), .pin7(_74161_4_pin14[1]), .pin8(_74161_4_pin14[2]),
    .pin9(_74161_4_pin14[3]), .pin10(1'b0), .pin11(FR_OUT_pin14[3]), .pin12(FR_OUT_pin14[2]),
    .pin13(FR_OUT_pin14[1]), .pin14(FR_OUT_pin14[0]), .pin15(FR_OUT_pin18[3]), .pin16(FR_OUT_pin18[2]),
    .pin17(FR_OUT_pin18[1]), .pin18(FR_OUT_pin18[0]), .pin19(not_EPC_H), .pin20(1'b1));
  _74245 _74245_3 (
    .pin1(1'b1), .pin2(_74161_1_pin14[0]), .pin3(_74161_1_pin14[1]), .pin4(_74161_1_pin14[2]),
    .pin5(_74161_1_pin14[3]), .pin6(_74161_2_pin14[0]), .pin7(_74161_2_pin14[1]), .pin8(_74161_2_pin14[2]),
    .pin9(_74161_2_pin14[3]), .pin10(1'b0), .pin11(MAR_L_pin19), .pin12(MAR_L_pin16), .pin13(MAR_L_pin15),
    .pin14(MAR_L_pin12), .pin15(MAR_L_pin9), .pin16(MAR_L_pin6), .pin17(MAR_L_pin5), .pin18(MAR_L_pin2),
    .pin19(not_EPC_RAM), .pin20(1'b1));
  _7404 _7404_2 (
    .pin1(1'b0), .pin3(1'b0), .pin5(1'b0), .pin7(1'b0), .pin9(1'b1), .pin11(1'b1), .pin12(_7404_2_pin12),
    .pin13(MAR_H_pin19), .pin14(1'b1));  // open: pin2, pin4, pin6, pin8, pin10
  _74245 _74245_4 (
    .pin1(1'b1), .pin2(_74161_3_pin14[0]), .pin3(_74161_3_pin14[1]), .pin4(_74161_3_pin14[2]),
    .pin5(_74161_3_pin14[3]), .pin6(_74161_4_pin14[0]), .pin7(_74161_4_pin14[1]), .pin8(_74161_4_pin14[2]),
    .pin9(_74161_4_pin14[3]), .pin10(1'b0), .pin11(MAR_H_pin19), .pin12(MAR_H_pin16), .pin13(MAR_H_pin15),
    .pin14(MAR_H_pin12), .pin15(MAR_H_pin9), .pin16(MAR_H_pin6), .pin17(MAR_H_pin5), .pin18(MAR_H_pin2),
    .pin19(not_EPC_RAM), .pin20(1'b1));
  // _28c256 ROM: pin names not known; wires that end beside it: MAR_H_pin16, MAR_H_pin12, MAR_L_pin19, MAR_L_pin16, MAR_L_pin15, MAR_L_pin12, MAR_L_pin9, MAR_L_pin6, MAR_L_pin5, MAR_L_pin2, FR_OUT_pin18[0], FR_OUT_pin18[1], FR_OUT_pin18[2], 1'b0, 1'b1, 1'b1, MAR_H_pin15, MAR_H_pin2, MAR_H_pin5, MAR_H_pin9, not_ERAM, MAR_H_pin6, MAR_H_pin19, FR_OUT_pin14[3]
  BusSplitter #(.Bits(16)) bussplitter_2 (
    .D(bussplitter_2_d), .OE(not_2_out), .D0(MAR_L_pin2), .D1(MAR_L_pin5), .D2(MAR_L_pin6), .D3(MAR_L_pin9),
    .D4(MAR_L_pin12), .D5(MAR_L_pin15), .D6(MAR_L_pin16), .D7(MAR_L_pin19), .D8(MAR_H_pin2), .D9(MAR_H_pin5),
    .D10(MAR_H_pin6), .D11(MAR_H_pin9), .D12(MAR_H_pin12), .D13(MAR_H_pin15), .D14(MAR_H_pin16),
    .D15(MAR_H_pin19));
  // _62256 RAM: pin names not known; wires that end beside it: MAR_H_pin16, MAR_H_pin12, MAR_L_pin19, MAR_L_pin16, MAR_L_pin15, MAR_L_pin12, MAR_L_pin9, MAR_L_pin6, MAR_L_pin5, MAR_L_pin2, FR_OUT_pin18[0], FR_OUT_pin18[1], FR_OUT_pin18[2], 1'b0, 1'b1, not_WRAM, MAR_H_pin15, MAR_H_pin2, MAR_H_pin5, MAR_H_pin9, not_ERAM, MAR_H_pin6, _7404_2_pin12, FR_OUT_pin14[3]
  _74245 _74245_5 (
    .pin1(1'b1), .pin2(1'b1), .pin3(1'b1), .pin4(1'b1), .pin5(1'b1), .pin6(1'b1), .pin7(1'b1), .pin8(1'b1),
    .pin9(1'b1), .pin10(1'b0), .pin11(MAR_H_pin19), .pin12(MAR_H_pin16), .pin13(MAR_H_pin15),
    .pin14(MAR_H_pin12), .pin15(MAR_H_pin9), .pin16(MAR_H_pin6), .pin17(MAR_H_pin5), .pin18(MAR_H_pin2),
    .pin19(not_ESP), .pin20(1'b1));
  Seven_Seg_Hex seven_seg_hex_7 (.d(_74245_6_pin9), .dp(1'b0));
  Seven_Seg_Hex seven_seg_hex_8 (.d(_74245_6_pin5), .dp(1'b0));
  _74245 _74245_6 (
    .pin1(1'b1), .pin2(_74245_6_pin5[0]), .pin3(_74245_6_pin5[1]), .pin4(_74245_6_pin5[2]),
    .pin5(_74245_6_pin5[3]), .pin6(_74245_6_pin9[0]), .pin7(_74245_6_pin9[1]), .pin8(_74245_6_pin9[2]),
    .pin9(_74245_6_pin9[3]), .pin10(1'b0), .pin11(MAR_L_pin19), .pin12(MAR_L_pin16), .pin13(MAR_L_pin15),
    .pin14(MAR_L_pin12), .pin15(MAR_L_pin9), .pin16(MAR_L_pin6), .pin17(MAR_L_pin5), .pin18(MAR_L_pin2),
    .pin19(not_ESP), .pin20(1'b1));
  _74191 _74191_1 (
    .pin1(1'b1), .pin2(_74245_6_pin5[1]), .pin3(_74245_6_pin5[0]), .pin4(not_CSP), .pin5(SPD),
    .pin6(_74245_6_pin5[2]), .pin7(_74245_6_pin5[3]), .pin8(1'b0), .pin9(1'b1), .pin10(1'b1),
    .pin11(not_CLR), .pin13(_74191_1_pin13), .pin14(Inc_T), .pin15(1'b1), .pin16(1'b1));  // open: pin12
  _74191 _74191_2 (
    .pin1(1'b1), .pin2(_74245_6_pin9[1]), .pin3(_74245_6_pin9[0]), .pin4(not_CSP), .pin5(SPD),
    .pin6(_74245_6_pin9[2]), .pin7(_74245_6_pin9[3]), .pin8(1'b0), .pin9(1'b1), .pin10(1'b1),
    .pin11(not_CLR), .pin14(_74191_1_pin13), .pin15(1'b1), .pin16(1'b1));  // open: pin12, pin13
  Seven_Seg_Hex seven_seg_hex_9 (.d(bussplitter_1_d[7:4]), .dp(1'b0));
  Seven_Seg_Hex seven_seg_hex_10 (.d(bussplitter_1_d[3:0]), .dp(1'b0));
  not not_1 (not_1_out, and_1_out);
  and and_1 (and_1_out, not_EINT_OUT, and_2_out);
  Seven_Seg_Hex seven_seg_hex_11 (.d(bussplitter_2_d[15:12]), .dp(1'b0));
  Seven_Seg_Hex seven_seg_hex_12 (.d(bussplitter_2_d[11:8]), .dp(1'b0));
  Seven_Seg_Hex seven_seg_hex_13 (.d(bussplitter_2_d[7:4]), .dp(1'b0));
  not not_2 (not_2_out, 1'b1);
  Seven_Seg_Hex seven_seg_hex_14 (.d(bussplitter_2_d[3:0]), .dp(1'b0));
  Seven_Seg_Hex seven_seg_hex_15 (.d(Control_Word__6_p16), .dp(1'b0));
  Seven_Seg_Hex seven_seg_hex_16 (.d(Control_Word__6_p15), .dp(1'b0));
  Seven_Seg_Hex seven_seg_hex_17 (.d({3'b000, Control_Word__6_p5[4]}), .dp(1'b0));
  Seven_Seg_Hex seven_seg_hex_18 (.d(Control_Word__6_p5[3:0]), .dp(1'b0));
  // SwitchDT switchdt_1: pin names not known; wires that end beside it: 1'b0, switchdt_1_p2, switchdt_1_p3
  // SwitchDT switchdt_2: pin names not known; wires that end beside it: 1'b0, switchdt_2_p2, switchdt_2_p3
  // SwitchDT switchdt_3: pin names not known; wires that end beside it: 1'b0, switchdt_3_p2, switchdt_3_p3
  Seven_Seg_Hex seven_seg_hex_19 (.d(OUT_pin12), .dp(1'b0));
  Seven_Seg_Hex seven_seg_hex_20 (.d(OUT_pin2), .dp(1'b0));
  // SwitchDT switchdt_4: pin names not known; wires that end beside it: INT1, 1'b1
  // _28c64 Instructions_Control_Word: pin names not known; wires that end beside it: 1'b1, 1'b1, Control_Word__6_p16[3], Control_Word__6_p15[2], Control_Word__6_p15[3], Control_Word__6_p15[1], Control_Word__6_p16[0], Control_Word__6_p15[0], Control_Word__6_p16[2], Control_Word__6_p5[4], 1'b0, Control_Word__6_p5[3], Control_Word__6_p16[1], Control_Word__6_p5[2], 1'b0, Control_Word__6_p5[1], Instructions_Control_Word_p17, Control_Word__6_p5[0], Instructions_Control_Word_p19, Instructions_Control_Word_p20, Instructions_Control_Word_p21, 1'b0
  // SwitchDT switchdt_5: pin names not known; wires that end beside it: INT2, 1'b1
  PullUp pullup_1 (.out(switchdt_1_p3));
  PullUp pullup_2 (.out(switchdt_2_p3));
  PullUp pullup_3 (.out(switchdt_3_p3));
  // _28c64 Registers_Control_Word: pin names not known; wires that end beside it: 1'b1, 1'b1, Control_Word__6_p16[3], Control_Word__6_p15[2], Control_Word__6_p15[3], Control_Word__6_p15[1], Control_Word__6_p16[0], Control_Word__6_p15[0], Control_Word__6_p16[2], Control_Word__6_p5[4], 1'b0, Control_Word__6_p5[3], Control_Word__6_p16[1], Control_Word__6_p5[2], 1'b0, Control_Word__6_p5[1], Control_Word__6_p5[0], Registers_Control_Word_p18, Registers_Control_Word_p19, Registers_Control_Word_p20, 1'b0
  PullUp pullup_4 (.out(switchdt_1_p2));
  PullUp pullup_5 (.out(switchdt_2_p2));
  PullUp pullup_6 (.out(switchdt_3_p2));
  _7400 Debouncer (
    .pin1(switchdt_1_p2), .pin2(CLR__not_used), .pin3(not_CLR), .pin4(not_CLR), .pin5(switchdt_1_p3),
    .pin6(CLR__not_used), .pin7(1'b0), .pin8(Debouncer_pin8), .pin9(switchdt_2_p3), .pin10(Debouncer_pin10),
    .pin11(Debouncer_pin10), .pin12(Debouncer_pin8), .pin13(switchdt_2_p2), .pin14(1'b1));
  _7400 Debouncer_2 (
    .pin1(switchdt_3_p2), .pin2(Debouncer_2_pin2), .pin3(Debouncer_2_pin3), .pin4(Debouncer_2_pin3),
    .pin5(switchdt_3_p3), .pin6(Debouncer_2_pin2), .pin7(1'b0), .pin8(Debouncer_2_pin8),
    .pin9(Debouncer_2_pin2), .pin10(Debouncer_2_pin10), .pin11(Debouncer_2_pin11), .pin12(Debouncer_2_pin12),
    .pin13(Debouncer_2_pin8), .pin14(1'b1));
  _7404 CLOCK_BUF (
    .pin1(Debouncer_2_pin11), .pin2(CLOCK_BUF_pin2), .pin3(CLOCK_BUF_pin2), .pin4(CLK),
    .pin5(Debouncer_2_pin11), .pin6(Inc_T), .pin7(1'b0), .pin9(1'b1), .pin10(EEPROM_ready),
    .pin11(CLOCK_BUF_pin11), .pin12(CLOCK_BUF_pin11), .pin13(CLOCK_BUF_pin13), .pin14(1'b1));  // open: pin8
  _7400 _7400_2 (
    .pin1(Debouncer_pin10), .pin2(Debouncer_2_pin3), .pin3(Debouncer_2_pin12), .pin4(Debouncer_2_pin11),
    .pin5(Debouncer_2_pin11), .pin6(_7400_2_pin6), .pin7(1'b0), .pin8(CLOCK_BUF_pin13), .pin9(_7400_2_pin6),
    .pin10(_7400_2_pin10), .pin11(_7400_2_pin10), .pin12(NE555___ext_CLK__to_do),
    .pin13(NE555___ext_CLK__to_do), .pin14(1'b1));
  _74107 _74107_1 (
    .pin1(not_HLT), .pin3(Debouncer_2_pin10), .pin4(not_HLT), .pin7(1'b0), .pin8(1'b0), .pin9(1'b0),
    .pin10(1'b0), .pin11(1'b0), .pin12(NE555___ext_CLK__to_do), .pin13(not_CLR), .pin14(1'b1));  // open: pin2, pin5, pin6
  _74138 _74138_1 (
    .pin1(_74138_1_pin1), .pin2(_74138_1_pin2), .pin3(_74138_1_pin3), .pin4(1'b0), .pin5(1'b0),
    .pin6(EEPROM_ready), .pin8(1'b0), .pin9(_74138_1_pin9), .pin10(_74138_1_pin10), .pin11(_74138_1_pin11),
    .pin12(_74138_1_pin12), .pin13(_74138_1_pin13), .pin14(_74138_1_pin14), .pin16(1'b1));  // open: pin7, pin15
  _74238 _74238_1 (
    .pin1(Registers_Control_Word_p18), .pin2(Registers_Control_Word_p19), .pin3(Registers_Control_Word_p20),
    .pin4(1'b0), .pin5(1'b0), .pin6(EEPROM_ready), .pin7(_74238_1_pin7), .pin8(1'b0), .pin9(_74238_1_pin9),
    .pin10(_74238_1_pin10), .pin11(_74238_1_pin11), .pin12(_74238_1_pin12), .pin13(_74238_1_pin13),
    .pin14(_74238_1_pin14), .pin16(1'b1));  // open: pin15
  _74373 _74373_1 (
    .pin1(1'b0), .pin2(LIR), .pin3(Instructions_Control_Word_p19), .pin4(Instructions_Control_Word_p20),
    .pin5(CHKI), .pin6(not_HLT), .pin7(Instructions_Control_Word_p21), .pin8(_74373_1_pin8),
    .pin9(not_ENA_I), .pin10(1'b0), .pin11(EEPROM_ready), .pin12(out_67), .pin13(_74373_1_pin13),
    .pin14(_74373_1_pin14), .pin15(not_EINT_OUT), .pin16(not_DIS_I), .pin17(_74373_1_pin17),
    .pin18(Instructions_Control_Word_p17), .pin19(not_NOP), .pin20(1'b1));
  and and_2 (and_2_out, _74138_1_pin9, _74138_1_pin10, _74138_1_pin11, _74138_1_pin12, _74138_1_pin13, _74138_1_pin14);
  BusSplitter #(.Bits(8)) bussplitter_3 (
    .D(bussplitter_1_d), .OE(and_2_out), .D0(bussplitter_3_d0), .D1(bussplitter_3_d1), .D2(bussplitter_3_d2),
    .D3(bussplitter_3_d3), .D4(bussplitter_3_d4), .D5(bussplitter_3_d5), .D6(bussplitter_3_d6),
    .D7(bussplitter_3_d7));
  _74373 A (
    .pin1(_74138_1_pin14), .pin2(bussplitter_3_d0), .pin3(bussplitter_3_d0), .pin4(bussplitter_3_d1),
    .pin5(bussplitter_3_d1), .pin6(bussplitter_3_d2), .pin7(bussplitter_3_d2), .pin8(bussplitter_3_d3),
    .pin9(bussplitter_3_d3), .pin10(1'b0), .pin11(_74238_1_pin14), .pin12(bussplitter_3_d4),
    .pin13(bussplitter_3_d4), .pin14(bussplitter_3_d5), .pin15(bussplitter_3_d5), .pin16(bussplitter_3_d6),
    .pin17(bussplitter_3_d6), .pin18(bussplitter_3_d7), .pin19(bussplitter_3_d7), .pin20(1'b1));
  _7408 _7408_3 (
    .pin1(not_CLR), .pin2(not_DIS_I), .pin3(_7408_3_pin3), .pin4(LIR), .pin5(_7408_3_pin5), .pin6(Load_IR),
    .pin7(1'b0), .pin8(Reset_IR), .pin9(not_CLR), .pin10(_7408_3_pin10), .pin11(Reset_T), .pin12(not_NOP),
    .pin13(not_CLR), .pin14(1'b1));
  _7474 I (
    .pin1(_7408_3_pin3), .pin2(1'b1), .pin3(1'b0), .pin4(not_ENA_I), .pin5(I_pin5), .pin7(1'b0),
    .pin9(I_pin9), .pin10(1'b1), .pin11(I_pin11), .pin12(1'b1), .pin13(not_ENA_I), .pin14(1'b1));  // open: pin6, pin8
  _74373 X (
    .pin1(_74138_1_pin13), .pin2(bussplitter_3_d0), .pin3(bussplitter_3_d0), .pin4(bussplitter_3_d1),
    .pin5(bussplitter_3_d1), .pin6(bussplitter_3_d2), .pin7(bussplitter_3_d2), .pin8(bussplitter_3_d3),
    .pin9(bussplitter_3_d3), .pin10(1'b0), .pin11(_74238_1_pin13), .pin12(bussplitter_3_d4),
    .pin13(bussplitter_3_d4), .pin14(bussplitter_3_d5), .pin15(bussplitter_3_d5), .pin16(bussplitter_3_d6),
    .pin17(bussplitter_3_d6), .pin18(bussplitter_3_d7), .pin19(bussplitter_3_d7), .pin20(1'b1));
  _7410 _7410_1 (
    .pin1(1'b0), .pin2(1'b0), .pin3(I_pin5), .pin4(I_pin9), .pin5(CHKI), .pin6(_7410_1_pin6), .pin7(1'b0),
    .pin8(I_pin11), .pin9(Int_NE555), .pin10(_7410_1_pin10), .pin11(_7410_1_pin11), .pin13(1'b1), .pin14(1'b1));  // open: pin12
  PullDown pulldown_1 (.out(INT1));
  PullDown pulldown_2 (.out(INT2));
  _7400 _7400_3 (
    .pin1(_7410_1_pin6), .pin2(_7410_1_pin6), .pin3(_7400_3_pin3), .pin4(EEPROM_ready), .pin5(EEPROM_ready),
    .pin6(_7408_3_pin5), .pin7(1'b0), .pin9(1'b1), .pin10(1'b1), .pin11(_7408_3_pin10), .pin12(_7408_3_pin5),
    .pin13(_7400_3_pin3), .pin14(1'b1));  // open: pin8
  _7474 ext_I (
    .pin1(not_ENA_I), .pin2(1'b1), .pin3(INT1), .pin4(1'b1), .pin5(ext_I_pin5), .pin6(_7410_1_pin11),
    .pin7(1'b0), .pin8(_7410_1_pin10), .pin9(ext_I_pin9), .pin10(1'b1), .pin11(INT2), .pin12(1'b1),
    .pin13(not_ENA_I), .pin14(1'b1));
  _74373 Y (
    .pin1(_74138_1_pin12), .pin2(bussplitter_3_d0), .pin3(bussplitter_3_d0), .pin4(bussplitter_3_d1),
    .pin5(bussplitter_3_d1), .pin6(bussplitter_3_d2), .pin7(bussplitter_3_d2), .pin8(bussplitter_3_d3),
    .pin9(bussplitter_3_d3), .pin10(1'b0), .pin11(_74238_1_pin12), .pin12(bussplitter_3_d4),
    .pin13(bussplitter_3_d4), .pin14(bussplitter_3_d5), .pin15(bussplitter_3_d5), .pin16(bussplitter_3_d6),
    .pin17(bussplitter_3_d6), .pin18(bussplitter_3_d7), .pin19(bussplitter_3_d7), .pin20(1'b1));
  _74245 INT_OUT (
    .pin1(1'b1), .pin2(ext_I_pin5), .pin3(ext_I_pin9), .pin4(1'b1), .pin5(1'b1), .pin6(1'b1), .pin7(1'b1),
    .pin8(1'b1), .pin9(1'b1), .pin10(1'b0), .pin11(bussplitter_1_d[7]), .pin12(bussplitter_1_d[6]),
    .pin13(bussplitter_1_d[5]), .pin14(bussplitter_1_d[4]), .pin15(bussplitter_1_d[3]),
    .pin16(bussplitter_1_d[2]), .pin17(bussplitter_1_d[1]), .pin18(bussplitter_1_d[0]), .pin19(not_EINT_OUT),
    .pin20(1'b1));
  _74163 IC_L (
    .pin1(Reset_T), .pin2(Inc_T), .pin3(1'b0), .pin4(1'b0), .pin5(1'b0), .pin6(1'b0), .pin7(1'b1),
    .pin8(1'b0), .pin9(not_JMP), .pin10(1'b1), .pin11(Control_Word__6_p5[3]), .pin12(Control_Word__6_p5[2]),
    .pin13(Control_Word__6_p5[1]), .pin14(Control_Word__6_p5[0]), .pin15(IC_L_pin15), .pin16(1'b1));
  _74163 IC_H (
    .pin1(Reset_T), .pin2(Inc_T), .pin3(1'b1), .pin4(1'b0), .pin5(1'b0), .pin6(1'b0), .pin7(1'b1),
    .pin8(1'b0), .pin9(not_JMP), .pin10(IC_L_pin15), .pin14(Control_Word__6_p5[4]), .pin16(1'b1));  // open: pin11, pin12, pin13, pin15
  _74373 TMP (
    .pin1(_74138_1_pin11), .pin2(bussplitter_3_d0), .pin3(bussplitter_3_d0), .pin4(bussplitter_3_d1),
    .pin5(bussplitter_3_d1), .pin6(bussplitter_3_d2), .pin7(bussplitter_3_d2), .pin8(bussplitter_3_d3),
    .pin9(bussplitter_3_d3), .pin10(1'b0), .pin11(_74238_1_pin11), .pin12(bussplitter_3_d4),
    .pin13(bussplitter_3_d4), .pin14(bussplitter_3_d5), .pin15(bussplitter_3_d5), .pin16(bussplitter_3_d6),
    .pin17(bussplitter_3_d6), .pin18(bussplitter_3_d7), .pin19(bussplitter_3_d7), .pin20(1'b1));
  _74373 D (
    .pin1(_74138_1_pin10), .pin2(bussplitter_3_d0), .pin3(bussplitter_3_d0), .pin4(bussplitter_3_d1),
    .pin5(bussplitter_3_d1), .pin6(bussplitter_3_d2), .pin7(bussplitter_3_d2), .pin8(bussplitter_3_d3),
    .pin9(bussplitter_3_d3), .pin10(1'b0), .pin11(_74238_1_pin10), .pin12(bussplitter_3_d4),
    .pin13(bussplitter_3_d4), .pin14(bussplitter_3_d5), .pin15(bussplitter_3_d5), .pin16(bussplitter_3_d6),
    .pin17(bussplitter_3_d6), .pin18(bussplitter_3_d7), .pin19(bussplitter_3_d7), .pin20(1'b1));
  _74273 IR (
    .pin1(Reset_IR), .pin2(Control_Word__6_p15[0]), .pin3(bussplitter_1_d[0]), .pin4(bussplitter_1_d[1]),
    .pin5(Control_Word__6_p15[1]), .pin6(Control_Word__6_p15[2]), .pin7(bussplitter_1_d[2]),
    .pin8(bussplitter_1_d[3]), .pin9(Control_Word__6_p15[3]), .pin10(1'b0), .pin11(Load_IR),
    .pin12(Control_Word__6_p16[0]), .pin13(bussplitter_1_d[4]), .pin14(bussplitter_1_d[5]),
    .pin15(Control_Word__6_p16[1]), .pin16(Control_Word__6_p16[2]), .pin17(bussplitter_1_d[6]),
    .pin18(bussplitter_1_d[7]), .pin19(Control_Word__6_p16[3]), .pin20(1'b1));
  _74373 E (
    .pin1(_74138_1_pin9), .pin2(bussplitter_3_d0), .pin3(bussplitter_3_d0), .pin4(bussplitter_3_d1),
    .pin5(bussplitter_3_d1), .pin6(bussplitter_3_d2), .pin7(bussplitter_3_d2), .pin8(bussplitter_3_d3),
    .pin9(bussplitter_3_d3), .pin10(1'b0), .pin11(_74238_1_pin9), .pin12(bussplitter_3_d4),
    .pin13(bussplitter_3_d4), .pin14(bussplitter_3_d5), .pin15(bussplitter_3_d5), .pin16(bussplitter_3_d6),
    .pin17(bussplitter_3_d6), .pin18(bussplitter_3_d7), .pin19(bussplitter_3_d7), .pin20(1'b1));
  _74373 OUT (
    .pin1(1'b0), .pin2(OUT_pin2[0]), .pin3(bussplitter_3_d0), .pin4(bussplitter_3_d1), .pin5(OUT_pin2[1]),
    .pin6(OUT_pin2[2]), .pin7(bussplitter_3_d2), .pin8(bussplitter_3_d3), .pin9(OUT_pin2[3]), .pin10(1'b0),
    .pin11(_74238_1_pin7), .pin12(OUT_pin12[0]), .pin13(bussplitter_3_d4), .pin14(bussplitter_3_d5),
    .pin15(OUT_pin12[1]), .pin16(OUT_pin12[2]), .pin17(bussplitter_3_d6), .pin18(bussplitter_3_d7),
    .pin19(OUT_pin12[3]), .pin20(1'b1));

  assign CLK_2 = CLK;
  assign not_CLK = Inc_T;
  assign not_CLK_2 = Inc_T;
  assign not_CLR_2 = not_CLR;
  assign not_HLT_2 = not_HLT;
  assign not_LPC_H = LPCH_Load;

  // Notes on the sheet:
  //   NE555___ext_CLK__to_do: Hz: 1000
  //   Int_NE555: Hz: 10
  //   Remove me
  //   when needed to
  //   add other board
  //   Data Bus
  //   Remove me
  //   when needed to
  //   write to bus
  //   Address Bus
  //   Control Bus (IC + t)
  //   Control Bus
  //   Clock & Ctrl board
  //   Registers board
  //   Instructions board
  //   CLEAR (push)
  //   STEP (push)
  //   MANUAL/AUTO (switch)
  //   Out Reg
  //   ext INT 1
  //   not CLR
  //   not HLT
  //   CLK
  //   not CLK
  //   EEPROM ready
  //   ext INT 2
  //   CLK/2
  //   EEPROM ready is activated 1/4 of cycle after CLK falling.
  //   Use this signal to react and avoid eeprom glitch
  //   Enable interrupt 
  //   on CLI
  //   Only for simulation
  //   Disable interrupt
  //   on SEI or CLR
  //   CHKI & INT Enabled 
  //   & INT value
  //   (nand)
  //   Timer INT
  //   IC reset (SR) is activated on NOP or CLR
  //   IC preset (PE) is activated on JMP signal to 
  //   jump to second part of uCode (T=16)
  //   IC inc (CP) is activated by falling CLK (not CLK)
  //   TODO: if not CLK is not used in other part, move the
  //   inverter on this board (7410 has available port to be used)
  //   Generate control bus
  //   CP is activated when a new istruction needs to be executed
  //   on EEPROM ready falling down
  //   MR is activated when interrupt must be handled, on EEPROM 
  //   ready falling down
  //   IC and IR clock signals (CP) are synced
  //   with EEPROM ready signal to avoid glitch
  //   IR reset (MR) is synced too
  //   IC reset and preset (SR/PE) are not synced 
  //   because 74163 is a synchonous counter and
  //   all actions are performed on CP signal
  //   contents of Control Word #3 (hex, n*v repeats v):
  //   /Users/Vittorio.Nardone/Documents/__private__/sap-project/roms/cw3-rom.hex false
  //   contents of Registers Control Word (hex, n*v repeats v):
  //   /Users/Vittorio.Nardone/Documents/__private__/sap-project/roms/cw7-rom.hex false
  //   contents of Control Word #2 (hex, n*v repeats v):
  //   /Users/Vittorio.Nardone/Documents/__private__/sap-project/roms/cw2-rom.hex false
  //   contents of ROM (hex, n*v repeats v):
  //   /Users/Vittorio.Nardone/Documents/__private__/sap-project/roms/kernel-rom.hex false
  //   contents of Control Word #1 (hex, n*v repeats v):
  //   /Users/Vittorio.Nardone/Documents/__private__/sap-project/roms/cw1-rom.hex false
  //   contents of Control Word #6 (hex, n*v repeats v):
  //   /Users/Vittorio.Nardone/Documents/__private__/sap-project/roms/cw6-rom.hex false
  //   contents of Control Word #5 (hex, n*v repeats v):
  //   /Users/Vittorio.Nardone/Documents/__private__/sap-project/roms/cw5-rom.hex false
  //   contents of Control Word #4 (hex, n*v repeats v):
  //   /Users/Vittorio.Nardone/Documents/__private__/sap-project/roms/cw4-rom.hex false
  //   contents of Instructions Control Word (hex, n*v repeats v):
  //   /Users/Vittorio.Nardone/Documents/__private__/sap-project/roms/cw8-rom.hex false
endmodule
